// Logisim project 4Bit_Register_Parallel_Load.circ as structural Verilog: 1 circuit, main circuit Bit4_Register_Parallel_Load
module Bit4_Register_Parallel_Load (
  input  I1,
  input  I2,
  input  I3,
  input  I4,
  input  Load,
  input  CP,
  input  Reset,
  output A1,
  output A2,
  output A3,
  output A4
);

  wire and_1_out, and_2_out, and_3_out, and_4_out, and_5_out, and_6_out, and_7_out, and_8_out,
       clocked_rs_flip_flop_1_p5, not_1_out, not_2_out, not_3_out, not_4_out;

  not not_1 (not_1_out, I1);
  not not_2 (not_2_out, I2);
  not not_3 (not_3_out, I3);
  not not_4 (not_4_out, I4);
  and and_1 (and_1_out, Load, I1);
  and and_2 (and_2_out, Load, not_1_out);
  and and_3 (and_3_out, Load, I2);
  and and_4 (and_4_out, Load, not_2_out);
  and and_5 (and_5_out, Load, I3);
  and and_6 (and_6_out, Load, not_3_out);
  and and_7 (and_7_out, Load, I4);
  and and_8 (and_8_out, Load, not_4_out);
  // Clocked_RS_Flip_Flop clocked_rs_flip_flop_1: pin names not known; wires that end beside it: and_1_out, CP, and_2_out, Reset, clocked_rs_flip_flop_1_p5, clocked_rs_flip_flop_1_p5, A1
  Clocked_RS_Flip_Flop clocked_rs_flip_flop_2 (
    .S(and_3_out), .CP(CP), .R(and_4_out), .Reset(Reset), .Q(A2));  // open: QBar
  Clocked_RS_Flip_Flop clocked_rs_flip_flop_3 (
    .S(and_5_out), .CP(CP), .R(and_6_out), .Reset(Reset), .Q(A3));  // open: QBar
  Clocked_RS_Flip_Flop clocked_rs_flip_flop_4 (
    .S(and_7_out), .CP(CP), .R(and_8_out), .Reset(Reset), .Q(A4));  // open: QBar
endmodule
