// Logisim project Clocked_RS_Flip_Flop.circ as structural Verilog: 1 circuit, main circuit Clocked_RS_Flip_Flop
module Clocked_RS_Flip_Flop (
  input  S,
  input  CP,
  input  R,
  input  Reset,
  output Q,
  output QBar
);

  wire nand_1_out, nand_2_out;

  nand nand_1 (nand_1_out, S, CP);
  nand nand_2 (nand_2_out, CP, R);
  nand nand_3 (Q, nand_1_out, QBar);
  nand nand_4 (QBar, Q, Reset, nand_2_out);

  // Notes on the sheet:
  //   R
endmodule
