// Logisim project Half_Adder.circ as structural Verilog: 1 circuit, main circuit Half_Adder
module Half_Adder (
  input  P,
  input  Q,
  output C,
  output S
);

  xor xor_1 (S, P, Q);
  and and_1 (C, P, Q);
endmodule
