// Logisim project 16BitMux4x1.circ as structural Verilog: 1 circuit, main circuit Bit16Mux4x1
module Bit16Mux4x1 (
  input  [15:0] I0,
  input  [15:0] I1,
  input  [15:0] I2,
  input  [15:0] I3,
  input  S0,
  input  S1,
  output [15:0] out_7
);

  wire [15:0] and_1_out, and_2_out, and_3_out, and_4_out, bit_extender_1_out, bit_extender_2_out, not_1_out,
       not_2_out;

  assign bit_extender_1_out = {{15{S0}}, S0};  // Bit_Extender bit_extender_1
  assign bit_extender_2_out = {{15{S1}}, S1};  // Bit_Extender bit_extender_2
  assign not_1_out = ~bit_extender_2_out;  // NOT_Gate not_1, 16 bits wide
  assign not_2_out = ~bit_extender_1_out;  // NOT_Gate not_2, 16 bits wide
  assign and_1_out = I0 & not_2_out & not_1_out;  // AND_Gate and_1, 16 bits wide
  assign and_2_out = I1 & bit_extender_1_out & not_1_out;  // AND_Gate and_2, 16 bits wide
  assign and_3_out = I2 & not_2_out & bit_extender_2_out;  // AND_Gate and_3, 16 bits wide
  assign and_4_out = I3 & bit_extender_1_out & bit_extender_2_out;  // AND_Gate and_4, 16 bits wide
  assign out_7 = and_1_out | and_2_out | and_3_out | and_4_out;  // OR_Gate or_1, 16 bits wide
endmodule
