// Logisim project 16Bit_Full_Adder.circ as structural Verilog: 2 circuits, main circuit Bit16_Half_Adder
module Bit16_Half_Adder (
  input  [15:0] P,
  input  [15:0] Q,
  output [15:0] C,
  output [15:0] S
);

  assign S = P ^ Q;  // XOR_Gate xor_1, 16 bits wide
  assign C = P & Q;  // AND_Gate and_1, 16 bits wide
endmodule

module Bit16_Full_Adder (
  input  [15:0] P,
  input  [15:0] Q,
  input  [15:0] R,
  output [15:0] C,
  output [15:0] S
);

  wire [15:0] bit16_half_adder_1_c, bit16_half_adder_1_s, bit16_half_adder_2_c;

  Bit16_Half_Adder bit16_half_adder_1 (.P(P), .Q(Q), .C(bit16_half_adder_1_c), .S(bit16_half_adder_1_s));
  Bit16_Half_Adder bit16_half_adder_2 (.P(bit16_half_adder_1_s), .Q(R), .C(bit16_half_adder_2_c), .S(S));
  assign C = bit16_half_adder_1_c | bit16_half_adder_2_c;  // OR_Gate or_1, 16 bits wide
endmodule
