// Logisim project 4Bit_Adder_Carry_Look_Ahead.circ as structural Verilog: 2 circuits, main circuit Logic_Circuit
module Logic_Circuit (
  input  P8,
  input  G8,
  input  P4,
  input  G4,
  input  P2,
  input  G2,
  input  P1,
  input  G1,
  input  C1,
  output C16,
  output C8,
  output C4,
  output C2
);

  wire and_1_out, and_2_out, and_3_out, and_4_out, and_5_out, and_6_out, and_7_out, and_8_out, and_9_out,
       and_10_out;

  and and_1 (and_1_out, C1, P8, P1, P2, P4);
  and and_2 (and_2_out, P8, G1, P4, P2);
  and and_3 (and_3_out, P4, G2, P8);
  and and_4 (and_4_out, G4, P8);
  and and_5 (and_5_out, C1, P1, P2, P4);
  and and_6 (and_6_out, P1, G1, P4);
  and and_7 (and_7_out, G2, P4);
  and and_8 (and_8_out, C1, P1, P2);
  and and_9 (and_9_out, G1, P2);
  and and_10 (and_10_out, C1, P1);
  or or_1 (C16, and_1_out, and_2_out, and_3_out, and_4_out, G8);
  or or_2 (C8, and_5_out, and_6_out, and_7_out, G4);
  or or_3 (C4, and_8_out, and_9_out, G2);
  or or_4 (C2, and_10_out, G1);

  // Notes on the sheet:
  //   C16 = G8 + P8C8
  //   C8 = G4 + P4G2 + P4P2G1 + P4P2P1C1
  //   C4 = G2 + P2G1 + P2P1C1
  //   C2 = G1 + P1C1
endmodule

module Bit4_Adder_Carry_Look_Ahead (
  input  B8,
  input  A8,
  input  B4,
  input  A4,
  input  B2,
  input  A2,
  input  B1,
  input  A1,
  input  C1,
  output C16,
  output S8,
  output S4,
  output S2,
  output S1
);

  wire half_adder_1_c, half_adder_1_s, half_adder_2_c, half_adder_2_s, half_adder_3_c, half_adder_3_s,
       half_adder_4_c, half_adder_4_s, logic_circuit_1_c2, logic_circuit_1_c4, logic_circuit_1_c8;

  Half_Adder half_adder_1 (.P(B8), .Q(A8), .C(half_adder_1_c), .S(half_adder_1_s));
  Half_Adder half_adder_2 (.P(B4), .Q(A4), .C(half_adder_2_c), .S(half_adder_2_s));
  Half_Adder half_adder_3 (.P(B2), .Q(A2), .C(half_adder_3_c), .S(half_adder_3_s));
  Half_Adder half_adder_4 (.P(B1), .Q(A1), .C(half_adder_4_c), .S(half_adder_4_s));
  Logic_Circuit logic_circuit_1 (
    .P8(half_adder_1_s), .G8(half_adder_1_c), .P4(half_adder_2_s), .G4(half_adder_2_c), .P2(half_adder_3_s),
    .G2(half_adder_3_c), .P1(half_adder_4_s), .G1(half_adder_4_c), .C1(C1), .C16(C16),
    .C8(logic_circuit_1_c8), .C4(logic_circuit_1_c4), .C2(logic_circuit_1_c2));
  xor xor_1 (S8, half_adder_1_s, logic_circuit_1_c8);
  xor xor_2 (S4, half_adder_2_s, logic_circuit_1_c4);
  xor xor_3 (S2, half_adder_3_s, logic_circuit_1_c2);
  xor xor_4 (S1, half_adder_4_s, C1);
endmodule
