// Logisim project 4Bit_Adder_Ripple.circ as structural Verilog: 3 circuits, main circuit Bit4NumberAdder
module halfAdder (
  input  P,
  input  Q,
  output C,
  output S
);

  xor xor_1 (S, P, Q);
  and and_1 (C, P, Q);
endmodule

module fullAdder (
  input  P,
  input  Q,
  input  R,
  output C,
  output S
);

  wire halfadder_1_c, halfadder_1_s, halfadder_2_c;

  halfAdder halfadder_1 (.P(P), .Q(Q), .C(halfadder_1_c), .S(halfadder_1_s));
  halfAdder halfadder_2 (.P(halfadder_1_s), .Q(R), .C(halfadder_2_c), .S(S));
  or or_1 (C, halfadder_1_c, halfadder_2_c);
endmodule

module Bit4NumberAdder (
  input  Q0,
  input  Q2,
  input  Q4,
  input  Q8,
  input  R0,
  input  R2,
  input  R4,
  input  R8,
  output C,
  output S0,
  output S2,
  output S4,
  output S8
);

  wire fulladder_1_c, fulladder_2_c, fulladder_3_c;

  fullAdder fulladder_1 (.P(1'b0), .Q(Q0), .R(R0), .C(fulladder_1_c), .S(S0));
  fullAdder fulladder_2 (.P(fulladder_1_c), .Q(Q2), .R(R2), .C(fulladder_2_c), .S(S2));
  fullAdder fulladder_3 (.P(fulladder_2_c), .Q(Q4), .R(R4), .C(fulladder_3_c), .S(S4));
  fullAdder fulladder_4 (.P(fulladder_3_c), .Q(Q8), .R(R8), .C(C), .S(S8));
endmodule
