// Logisim project 4Bit_Counter.circ as structural Verilog: 1 circuit, main circuit Bit4_Counter
module Bit4_Counter (
  input  INR,
  input  CP,
  input  CLR,
  output A0,
  output A1,
  output A2,
  output A3
);

  wire and_1_out, and_2_out, and_3_out, and_4_out, and_5_out, master_slave_flip_flop_2_p2,
       master_slave_flip_flop_3_p2, master_slave_flip_flop_4_p2, not_1_out, or_1_out, or_2_out, or_3_out,
       or_4_out;

  not not_1 (not_1_out, CLR);
  and and_1 (and_1_out, INR, not_1_out);
  or or_1 (or_1_out, INR, CLR);
  and and_2 (and_2_out, INR, not_1_out);
  or or_2 (or_2_out, INR, CLR);
  and and_3 (and_3_out, INR, not_1_out);
  or or_3 (or_3_out, INR, CLR);
  and and_4 (and_4_out, INR, not_1_out);
  or or_4 (or_4_out, INR, CLR);
  and and_5 (and_5_out, CP, CLR);
  // Master_Slave_Flip_Flop master_slave_flip_flop_1: pin names not known; wires that end beside it: and_1_out, CP, or_1_out, or_1_out, A0
  // Master_Slave_Flip_Flop master_slave_flip_flop_2: pin names not known; wires that end beside it: and_2_out, master_slave_flip_flop_2_p2, or_2_out, or_2_out, A1
  // Master_Slave_Flip_Flop master_slave_flip_flop_3: pin names not known; wires that end beside it: and_3_out, master_slave_flip_flop_3_p2, or_3_out, or_3_out, A2
  // Master_Slave_Flip_Flop master_slave_flip_flop_4: pin names not known; wires that end beside it: and_4_out, master_slave_flip_flop_4_p2, or_4_out, or_4_out, A3
  or or_5 (master_slave_flip_flop_2_p2, A0, and_5_out);
  or or_6 (master_slave_flip_flop_3_p2, A1, and_5_out);
  or or_7 (master_slave_flip_flop_4_p2, A2, and_5_out);
endmodule
