// Logisim project Binary_Ripple_Counter_JK.circ as structural Verilog: 1 circuit, main circuit main
module main (
  input  CP,
  output A0,
  output A1,
  output A2,
  output A4
);

  // Master_Slave_Flip_Flop master_slave_flip_flop_1: pin names not known; wires that end beside it: 1'b1, CP, 1'b1, A0
  // Master_Slave_Flip_Flop master_slave_flip_flop_2: pin names not known; wires that end beside it: 1'b1, A0, 1'b1, A1
  // Master_Slave_Flip_Flop master_slave_flip_flop_3: pin names not known; wires that end beside it: 1'b1, A1, 1'b1, A2
  // Master_Slave_Flip_Flop master_slave_flip_flop_4: pin names not known; wires that end beside it: 1'b1, A2, 1'b1, A4
endmodule
