// Logisim project Counter42513.circ as structural Verilog: 2 circuits, main circuit main
module main (
  input  Reset,
  output A,
  output B,
  output C
);

  wire combinationalcircuit_1_ja, combinationalcircuit_1_jb, combinationalcircuit_1_jc,
       combinationalcircuit_1_ka, combinationalcircuit_1_kb, combinationalcircuit_1_kc, CP_out;

  CombinationalCircuit combinationalcircuit_1 (
    .A(A), .B(B), .C(C), .JA(combinationalcircuit_1_ja), .KA(combinationalcircuit_1_ka),
    .JB(combinationalcircuit_1_jb), .KB(combinationalcircuit_1_kb), .KC(combinationalcircuit_1_kc),
    .JC(combinationalcircuit_1_jc));
  Clock CP (.out(CP_out));
  J_K_Flip_Flop j_k_ff_1 (
    .J(combinationalcircuit_1_ja), .K(combinationalcircuit_1_ka), .clk(CP_out), .Q(A), .reset(Reset));  // open: Qn, preset
  J_K_Flip_Flop j_k_ff_2 (
    .J(combinationalcircuit_1_jb), .K(combinationalcircuit_1_kb), .clk(CP_out), .Q(B), .reset(Reset));  // open: Qn, preset
  J_K_Flip_Flop j_k_ff_3 (
    .J(combinationalcircuit_1_jc), .K(combinationalcircuit_1_kc), .clk(CP_out), .Q(C), .reset(Reset));  // open: Qn, preset

  // Notes on the sheet:
  //   Design and simulate a self startinng synchronous binary counter that repeateadly counts the sequence 4 2 5 1 3 using JK FF
endmodule

module CombinationalCircuit (
  input  A,
  input  B,
  input  C,
  output JA,
  output KA,
  output JB,
  output KB,
  output KC,
  output JC
);

  wire not_1_out, not_2_out, or_2_out, or_3_out;

  not not_1 (not_1_out, C);
  not not_2 (not_2_out, A);
  or or_1 (JA, A, B, not_1_out);
  and and_1 (KC, not_2_out, B, C);
  and and_2 (JC, not_2_out, not_1_out, B);
  or or_2 (or_2_out, A, B, C);
  or or_3 (or_3_out, not_2_out, B, not_1_out);
  and and_3 (JB, or_2_out, or_3_out);

  assign KA = 1'b1;
  assign KB = 1'b1;
endmodule
