// Logisim project D_Flip_Flop.circ as structural Verilog: 1 circuit, main circuit main
module main (
  input  D,
  input  CP,
  output Q,
  output QBar
);

  wire nand_1_out, nand_2_out, nand_3_out, not_1_out, por_1_out;

  nand nand_1 (nand_1_out, D, D);
  POR por_1 (.out(por_1_out));
  not not_1 (not_1_out, por_1_out);
  nand nand_2 (nand_2_out, D, CP);
  nand nand_3 (nand_3_out, CP, nand_1_out);
  nand nand_4 (Q, nand_2_out, QBar);
  nand nand_5 (QBar, Q, not_1_out, nand_3_out);
endmodule
