// Logisim project Decoders.circ as structural Verilog: 3 circuits, main circuit Decoder2x4
module Decoder2x4 (
  input  S0,
  input  S1,
  output D0,
  output D1,
  output D2,
  output D3
);

  wire not_1_out, not_2_out;

  not not_1 (not_1_out, S1);
  not not_2 (not_2_out, S0);
  and and_1 (D0, not_2_out, not_1_out);
  and and_2 (D1, S0, not_1_out);
  and and_3 (D2, S1, not_2_out);
  and and_4 (D3, S1, S0);
endmodule

module Decoder3x8 (
  input  S0,
  input  S1,
  input  S2,
  output D0,
  output D1,
  output D2,
  output D3,
  output D4,
  output D5,
  output D6,
  output D7
);

  wire not_1_out, not_2_out, not_3_out;

  not not_1 (not_1_out, S0);
  not not_2 (not_2_out, S1);
  not not_3 (not_3_out, S2);
  and and_1 (D0, not_3_out, not_2_out, not_1_out);
  and and_2 (D1, not_3_out, not_2_out, S0);
  and and_3 (D2, not_3_out, S1, not_1_out);
  and and_4 (D3, not_3_out, S1, S0);
  and and_5 (D4, not_1_out, not_2_out, S2);
  and and_6 (D5, S2, not_2_out, S0);
  and and_7 (D6, S2, S1, not_1_out);
  and and_8 (D7, S2, S1, S0);
endmodule

module Decoder4x16 (
  input  S0,
  input  S1,
  input  S2,
  input  S3,
  output D0,
  output D1,
  output D2,
  output D3,
  output D4,
  output D5,
  output D6,
  output D7,
  output D8,
  output D9,
  output D10,
  output D11,
  output D12,
  output D13,
  output D14,
  output D15
);

  wire decoder3x8_1_d0, decoder3x8_1_d1, decoder3x8_1_d2, decoder3x8_1_d3, decoder3x8_1_d4, decoder3x8_1_d5,
       decoder3x8_1_d6, decoder3x8_1_d7, decoder3x8_2_d0, decoder3x8_2_d1, decoder3x8_2_d2, decoder3x8_2_d3,
       decoder3x8_2_d4, decoder3x8_2_d5, decoder3x8_2_d6, decoder3x8_2_d7, not_1_out;

  not not_1 (not_1_out, S3);
  Decoder3x8 decoder3x8_1 (
    .S0(S0), .S1(S1), .S2(S2), .D0(decoder3x8_1_d0), .D1(decoder3x8_1_d1), .D2(decoder3x8_1_d2),
    .D3(decoder3x8_1_d3), .D4(decoder3x8_1_d4), .D5(decoder3x8_1_d5), .D6(decoder3x8_1_d6),
    .D7(decoder3x8_1_d7));
  Decoder3x8 decoder3x8_2 (
    .S0(S0), .S1(S1), .S2(S2), .D0(decoder3x8_2_d0), .D1(decoder3x8_2_d1), .D2(decoder3x8_2_d2),
    .D3(decoder3x8_2_d3), .D4(decoder3x8_2_d4), .D5(decoder3x8_2_d5), .D6(decoder3x8_2_d6),
    .D7(decoder3x8_2_d7));
  and and_1 (D0, decoder3x8_1_d0, not_1_out);
  and and_2 (D1, decoder3x8_1_d1, not_1_out);
  and and_3 (D2, decoder3x8_1_d2, not_1_out);
  and and_4 (D3, decoder3x8_1_d3, not_1_out);
  and and_5 (D4, decoder3x8_1_d4, not_1_out);
  and and_6 (D5, decoder3x8_1_d5, not_1_out);
  and and_7 (D6, decoder3x8_1_d6, not_1_out);
  and and_8 (D7, decoder3x8_1_d7, not_1_out);
  and and_9 (D8, decoder3x8_2_d0, S3);
  and and_10 (D9, decoder3x8_2_d1, S3);
  and and_11 (D10, decoder3x8_2_d2, S3);
  and and_12 (D11, decoder3x8_2_d3, S3);
  and and_13 (D12, decoder3x8_2_d4, S3);
  and and_14 (D13, decoder3x8_2_d5, S3);
  and and_15 (D14, decoder3x8_2_d6, S3);
  and and_16 (D15, decoder3x8_2_d7, S3);
endmodule
