// Logisim project FinalPractical.circ as structural Verilog: 2 circuits, main circuit QuickWork
module QuickWork (
  input  I,
  output O
);

  wire CP_out, d_ff_1_q, d_ff_2_q, d_ff_3_q, d_ff_4_q, not_1_out, Reset_out;

  Clock CP (.out(CP_out));
  Button Reset (.out(Reset_out));
  D_Flip_Flop d_ff_1 (.D(I), .clk(CP_out), .Q(d_ff_1_q), .reset(Reset_out));  // open: Qn, preset
  D_Flip_Flop d_ff_2 (.D(d_ff_1_q), .clk(CP_out), .Q(d_ff_2_q), .reset(Reset_out));  // open: Qn, preset
  D_Flip_Flop d_ff_3 (.D(d_ff_2_q), .clk(CP_out), .Q(d_ff_3_q), .reset(Reset_out));  // open: Qn, preset
  D_Flip_Flop d_ff_4 (.D(d_ff_3_q), .clk(CP_out), .Q(d_ff_4_q), .reset(Reset_out));  // open: Qn, preset
  not not_1 (not_1_out, d_ff_4_q);
  nor nor_1 (O, d_ff_1_q, d_ff_2_q, d_ff_3_q, not_1_out);
endmodule

module Correct (
  input  X,
  output Y
);

  wire and_1_out, and_3_out, and_4_out, CP_out, not_1_out, not_2_out, not_3_out, or_1_out, or_2_out,
       Reset_out, S0_q, S1_q;

  not not_1 (not_1_out, X);
  not not_2 (not_2_out, S1_q);
  not not_3 (not_3_out, X);
  and and_1 (and_1_out, not_1_out, not_2_out, S0_q);
  or or_1 (or_1_out, not_2_out, S0_q, X);
  and and_2 (Y, S1_q, S0_q, not_3_out);
  Clock CP (.out(CP_out));
  Button Reset (.out(Reset_out));
  J_K_Flip_Flop S1 (.J(and_1_out), .K(or_1_out), .clk(CP_out), .Q(S1_q), .reset(Reset_out));  // open: Qn, preset
  and and_3 (and_3_out, not_2_out, X);
  and and_4 (and_4_out, S1_q, not_3_out);
  or or_2 (or_2_out, and_3_out, and_4_out);
  J_K_Flip_Flop S0 (.J(or_2_out), .K(1'b1), .clk(CP_out), .Q(S0_q), .reset(Reset_out));  // open: Qn, preset
endmodule
