// Logisim project Full_Adder.circ as structural Verilog: 1 circuit, main circuit Full_Adder
module Full_Adder (
  input  P,
  input  Q,
  input  R,
  output C,
  output S
);

  wire half_adder_1_c, half_adder_1_s, half_adder_2_c;

  Half_Adder half_adder_1 (.P(P), .Q(Q), .C(half_adder_1_c), .S(half_adder_1_s));
  Half_Adder half_adder_2 (.P(half_adder_1_s), .Q(R), .C(half_adder_2_c), .S(S));
  or or_1 (C, half_adder_1_c, half_adder_2_c);
endmodule
