// Logisim project Master_Slave_JK_Flip_Flop.circ as structural Verilog: 1 circuit, main circuit Master_Slave_Flip_Flop
module Master_Slave_Flip_Flop (
  input  J,
  input  K,
  input  CP,
  input  Reset,
  output Q,
  output QBar
);

  wire nand_1_out, nand_2_out, nand_3_out, nand_4_out, nand_5_out, nand_6_out, nand_7_out, not_1_out;

  not not_1 (not_1_out, Reset);
  nand nand_1 (nand_1_out, QBar, J, CP);
  nand nand_2 (nand_2_out, CP, K, Q);
  nand nand_3 (nand_3_out, CP, CP);
  nand nand_4 (nand_4_out, nand_1_out, nand_5_out);
  nand nand_5 (nand_5_out, nand_4_out, not_1_out, nand_2_out);
  nand nand_6 (nand_6_out, nand_3_out, nand_4_out);
  nand nand_7 (nand_7_out, nand_5_out, nand_3_out);
  nand nand_8 (Q, nand_6_out, QBar);
  nand nand_9 (QBar, Q, not_1_out, nand_7_out);

  // Notes on the sheet:
  //   By convention R=1 should reset the circuit to Q=0
  //   Maskter Slave JK Flip Flop
endmodule
