// Logisim project Mux8x1.circ as structural Verilog: 1 circuit, main circuit Mux8x1
module Mux8x1 (
  input  I0,
  input  I1,
  input  I2,
  input  I3,
  input  I4,
  input  I5,
  input  I6,
  input  I7,
  input  S0,
  input  S1,
  input  S2,
  output Y
);

  wire and_1_out, and_2_out, mux4x1_1_y, mux4x1_2_y, not_1_out;

  Mux4x1 mux4x1_1 (.I0(I0), .I1(I1), .I2(I2), .I3(I3), .S1(S0), .S0(S1), .Y(mux4x1_1_y));
  Mux4x1 mux4x1_2 (.I0(I4), .I1(I5), .I2(I6), .I3(I7), .S1(S0), .S0(S1), .Y(mux4x1_2_y));
  not not_1 (not_1_out, S2);
  and and_1 (and_1_out, not_1_out, mux4x1_1_y);
  and and_2 (and_2_out, mux4x1_2_y, S2);
  or or_1 (Y, and_1_out, and_2_out);
endmodule
