// Logisim project Registers.circ as structural Verilog: 4 circuits, main circuit Bit8_Register
module Bit8_Register (
  input  I0,
  input  I1,
  input  I2,
  input  I3,
  input  I4,
  input  I5,
  input  I6,
  input  I7,
  input  Load,
  input  CP,
  input  Reset,
  output A0,
  output A1,
  output A2,
  output A3,
  output A4,
  output A5,
  output A6,
  output A7
);

  Bit4_Register bit4_register_1 (
    .I0(I0), .I1(I1), .I2(I2), .I3(I3), .Load(Load), .CP(CP), .CLR(Reset), .A0(A0), .A1(A1), .A2(A2), .A3(A3));
  Bit4_Register bit4_register_2 (
    .I0(I4), .I1(I5), .I2(I6), .I3(I7), .Load(Load), .CP(CP), .CLR(Reset), .A0(A4), .A1(A5), .A2(A6), .A3(A7));
endmodule

module Bit12_Register (
  input  I0,
  input  I1,
  input  I2,
  input  I3,
  input  I4,
  input  I5,
  input  I6,
  input  I7,
  input  I8,
  input  I9,
  input  I10,
  input  I11,
  input  Load,
  input  CP,
  input  Reset,
  output A0,
  output A1,
  output A2,
  output A3,
  output A4,
  output A5,
  output A6,
  output A7,
  output A8,
  output A9,
  output A10,
  output A11
);

  Bit4_Register bit4_register_1 (
    .I0(I0), .I1(I1), .I2(I2), .I3(I3), .Load(Load), .CP(CP), .CLR(Reset), .A0(A0), .A1(A1), .A2(A2), .A3(A3));
  Bit4_Register bit4_register_2 (
    .I0(I4), .I1(I5), .I2(I6), .I3(I7), .Load(Load), .CP(CP), .CLR(Reset), .A0(A4), .A1(A5), .A2(A6), .A3(A7));
  Bit4_Register bit4_register_3 (
    .I0(I8), .I1(I9), .I2(I10), .I3(I11), .Load(Load), .CP(CP), .CLR(Reset), .A0(A8), .A1(A9), .A2(A10),
    .A3(A11));
endmodule

module Bit16_Register (
  input  I0,
  input  I1,
  input  I2,
  input  I3,
  input  I4,
  input  I5,
  input  I6,
  input  I7,
  input  I8,
  input  I9,
  input  I10,
  input  I11,
  input  I12,
  input  I13,
  input  I14,
  input  I15,
  input  Load,
  input  CP,
  input  Reset,
  output A0,
  output A1,
  output A2,
  output A3,
  output A4,
  output A5,
  output A6,
  output A7,
  output A8,
  output A9,
  output A10,
  output A11,
  output A12,
  output A13,
  output A14,
  output A15
);

  Bit4_Register bit4_register_1 (
    .I0(I0), .I1(I1), .I2(I2), .I3(I3), .Load(Load), .CP(CP), .CLR(Reset), .A0(A0), .A1(A1), .A2(A2), .A3(A3));
  Bit4_Register bit4_register_2 (
    .I0(I4), .I1(I5), .I2(I6), .I3(I7), .Load(Load), .CP(CP), .CLR(Reset), .A0(A4), .A1(A5), .A2(A6), .A3(A7));
  Bit4_Register bit4_register_3 (
    .I0(I8), .I1(I9), .I2(I10), .I3(I11), .Load(Load), .CP(CP), .CLR(Reset), .A0(A8), .A1(A9), .A2(A10),
    .A3(A11));
  Bit4_Register bit4_register_4 (
    .I0(I12), .I1(I13), .I2(I14), .I3(I15), .Load(Load), .CP(CP), .CLR(Reset), .A0(A12), .A1(A13), .A2(A14),
    .A3(A15));
endmodule

module Bit4_Register (
  input  I0,
  input  I1,
  input  I2,
  input  I3,
  input  Load,
  input  CP,
  input  CLR,
  output A0,
  output A1,
  output A2,
  output A3
);

  wire and_1_out, and_2_out, and_3_out, and_4_out, and_5_out, and_6_out, and_7_out, and_8_out, and_9_out,
       and_10_out, and_11_out, and_12_out, not_1_out, not_2_out, not_3_out, not_4_out, not_5_out, or_1_out,
       or_2_out, or_3_out, or_4_out;

  not not_1 (not_1_out, I0);
  not not_2 (not_2_out, I1);
  not not_3 (not_3_out, I2);
  not not_4 (not_4_out, I3);
  and and_1 (and_1_out, Load, I0);
  and and_2 (and_2_out, Load, not_1_out);
  and and_3 (and_3_out, Load, I1);
  and and_4 (and_4_out, Load, not_2_out);
  and and_5 (and_5_out, Load, I2);
  and and_6 (and_6_out, Load, not_3_out);
  and and_7 (and_7_out, Load, I3);
  and and_8 (and_8_out, Load, not_4_out);
  not not_5 (not_5_out, CLR);
  and and_9 (and_9_out, not_5_out, and_1_out);
  or or_1 (or_1_out, and_2_out, CLR);
  and and_10 (and_10_out, not_5_out, and_3_out);
  or or_2 (or_2_out, and_4_out, CLR);
  and and_11 (and_11_out, not_5_out, and_5_out);
  or or_3 (or_3_out, and_6_out, CLR);
  and and_12 (and_12_out, not_5_out, and_7_out);
  or or_4 (or_4_out, and_8_out, CLR);
  Clocked_RS_Flip_Flop clocked_rs_flip_flop_1 (
    .S(and_9_out), .CP(CP), .R(or_1_out), .Reset(or_1_out), .Q(A0));  // open: QBar
  Clocked_RS_Flip_Flop clocked_rs_flip_flop_2 (
    .S(and_10_out), .CP(CP), .R(or_2_out), .Reset(or_2_out), .Q(A1));  // open: QBar
  Clocked_RS_Flip_Flop clocked_rs_flip_flop_3 (
    .S(and_11_out), .CP(CP), .R(or_3_out), .Reset(or_3_out), .Q(A2));  // open: QBar
  Clocked_RS_Flip_Flop clocked_rs_flip_flop_4 (
    .S(and_12_out), .CP(CP), .R(or_4_out), .Reset(or_4_out), .Q(A3));  // open: QBar

  // Notes on the sheet:
  //   Had to use sychornous CLR to prevent timing issues.
endmodule
