// Logisim project SR_Flip_Flop.circ as structural Verilog: 1 circuit, main circuit main
module main (
  input  S,
  input  R,
  output Q,
  output QBar
);

  wire por_1_out;

  POR por_1 (.out(por_1_out));
  nor nor_1 (Q, S, por_1_out, QBar);
  nor nor_2 (QBar, Q, R);
endmodule
