// Logisim project T_Flip_Flop.circ as structural Verilog: 1 circuit, main circuit main
module main (
  input  T,
  input  CP,
  input  Reset,
  output Q,
  output QBar
);

  JK_Flip_Flop jk_flip_flop_1 (.K(T), .CP(CP), .J(T), .Reset(Reset), .Q(Q), .QBar(QBar));
endmodule
