// Logisim project 16Bit_Adder.circ as structural Verilog: 1 circuit, main circuit Bit16_Adder
module Bit16_Adder (
  input  C0,
  input  B3,
  input  B7,
  input  B11,
  input  B15,
  input  A3,
  input  A7,
  input  A11,
  input  A15,
  input  B2,
  input  B6,
  input  B10,
  input  B14,
  input  A2,
  input  A6,
  input  A10,
  input  A14,
  input  B1,
  input  B5,
  input  B9,
  input  B13,
  input  A1,
  input  A5,
  input  A9,
  input  A13,
  input  B0,
  input  B4,
  input  B8,
  input  B12,
  input  A0,
  input  A4,
  input  A8,
  input  A12,
  output S0,
  output S1,
  output S2,
  output S3,
  output S4,
  output S5,
  output S6,
  output s7,
  output S8,
  output S9,
  output S10,
  output S11,
  output S12,
  output S13,
  output S14,
  output S15,
  output S16
);

  wire bit4_adder_carry_look_ahead_1_c16, bit4_adder_carry_look_ahead_2_c16,
       bit4_adder_carry_look_ahead_3_c16;

  Bit4_Adder_Carry_Look_Ahead bit4_adder_carry_look_ahead_1 (
    .B8(B3), .A8(A3), .B4(B2), .A4(A2), .B2(B1), .A2(A1), .B1(B0), .A1(A0), .C1(C0),
    .C16(bit4_adder_carry_look_ahead_1_c16), .S8(S3), .S4(S2), .S2(S1), .S1(S0));
  Bit4_Adder_Carry_Look_Ahead bit4_adder_carry_look_ahead_2 (
    .B8(B7), .A8(A7), .B4(B6), .A4(A6), .B2(B5), .A2(A5), .B1(B4), .A1(A4),
    .C1(bit4_adder_carry_look_ahead_1_c16), .C16(bit4_adder_carry_look_ahead_2_c16), .S8(s7), .S4(S6),
    .S2(S5), .S1(S4));
  Bit4_Adder_Carry_Look_Ahead bit4_adder_carry_look_ahead_3 (
    .B8(B11), .A8(A11), .B4(B10), .A4(A10), .B2(B9), .A2(A9), .B1(B8), .A1(A8),
    .C1(bit4_adder_carry_look_ahead_2_c16), .C16(bit4_adder_carry_look_ahead_3_c16), .S8(S11), .S4(S10),
    .S2(S9), .S1(S8));
  Bit4_Adder_Carry_Look_Ahead bit4_adder_carry_look_ahead_4 (
    .B8(B15), .A8(A15), .B4(B14), .A4(A14), .B2(B13), .A2(A13), .B1(B12), .A1(A12),
    .C1(bit4_adder_carry_look_ahead_3_c16), .C16(S16), .S8(S15), .S4(S14), .S2(S13), .S1(S12));
endmodule
