// Logisim project Counter42513.circ as structural Verilog: 3 circuits, main circuit main
module main (
  input  Reset,
  output A,
  output B,
  output C
);

  wire combinationalcircuit_1_ja, combinationalcircuit_1_jb, combinationalcircuit_1_jc,
       combinationalcircuit_1_ka, combinationalcircuit_1_kb, combinationalcircuit_1_kc, CP_out;

  CombinationalCircuit combinationalcircuit_1 (
    .A(A), .B(B), .C(C), .JA(combinationalcircuit_1_ja), .KA(combinationalcircuit_1_ka),
    .JB(combinationalcircuit_1_jb), .KB(combinationalcircuit_1_kb), .KC(combinationalcircuit_1_kc),
    .JC(combinationalcircuit_1_jc));
  Clock CP (.out(CP_out));
  J_K_Flip_Flop j_k_ff_1 (
    .J(combinationalcircuit_1_ja), .K(combinationalcircuit_1_ka), .clk(CP_out), .Q(A), .reset(Reset));  // open: Qn, preset
  J_K_Flip_Flop j_k_ff_2 (
    .J(combinationalcircuit_1_jb), .K(combinationalcircuit_1_kb), .clk(CP_out), .Q(B), .reset(Reset));  // open: Qn, preset
  J_K_Flip_Flop j_k_ff_3 (
    .J(combinationalcircuit_1_jc), .K(combinationalcircuit_1_kc), .clk(CP_out), .Q(C), .reset(Reset));  // open: Qn, preset

  // Notes on the sheet:
  //   Design and simulate a self startinng synchronous binary counter that repeateadly counts the sequence 4 2 5 1 3 using JK FF
endmodule

module JK_Flip_Flop (
  input  in_1,
  input  in_2,
  input  in_3,
  input  in_4,
  input  in_5,
  input  in_6
);

  wire nand_1_out, nand_2_out;

  nand nand_1 (nand_1_out, in_4, in_1, in_3);
  nand nand_2 (nand_2_out, in_3, in_5, in_2);
  nand nand_3 (in_2, nand_1_out, in_4);
  nand nand_4 (in_4, in_2, in_6, nand_2_out);
endmodule

module CombinationalCircuit (
  input  A,
  input  B,
  input  C,
  output JA,
  output KA,
  output JB,
  output KB,
  output KC,
  output JC
);

  wire not_1_out, not_2_out, or_2_out, or_3_out;

  not not_1 (not_1_out, C);
  not not_2 (not_2_out, A);
  or or_1 (JA, A, B, not_1_out);
  and and_1 (KC, not_2_out, B, C);
  and and_2 (JC, not_2_out, not_1_out, B);
  or or_2 (or_2_out, A, B, C);
  or or_3 (or_3_out, not_2_out, B, not_1_out);
  and and_3 (JB, or_2_out, or_3_out);

  assign KA = 1'b1;
  assign KB = 1'b1;
endmodule
