// Logisim project JK_Flip_Flop.circ as structural Verilog: 1 circuit, main circuit JK_Flip_Flop
module JK_Flip_Flop (
  input  K,
  input  CP,
  input  J,
  input  Reset,
  output Q,
  output QBar
);

  wire and_1_out, and_2_out, not_1_out;

  and and_1 (and_1_out, Q, K, CP);
  and and_2 (and_2_out, CP, J, QBar);
  not not_1 (not_1_out, Reset);
  nor nor_1 (Q, and_1_out, QBar);
  nor nor_2 (QBar, Q, not_1_out, and_2_out);
endmodule
