// Logisim project Memory_Cell.circ as structural Verilog: 1 circuit, main circuit Memory_Cell
module Memory_Cell (
  input  I,
  input  CP,
  input  Reset,
  input  S,
  input  Read,
  output O
);

  wire and_1_out, and_2_out, clocked_rs_flip_flop_1_q, not_1_out, not_2_out;

  not not_1 (not_1_out, I);
  and and_1 (and_1_out, S, I, not_2_out);
  and and_2 (and_2_out, S, not_1_out, not_2_out);
  not not_2 (not_2_out, Read);
  Clocked_RS_Flip_Flop clocked_rs_flip_flop_1 (
    .S(and_1_out), .CP(CP), .R(and_2_out), .Reset(Reset), .Q(clocked_rs_flip_flop_1_q));  // open: QBar
  and and_3 (O, S, clocked_rs_flip_flop_1_q, Read);
endmodule
