// Logisim project Mux4x1.circ as structural Verilog: 1 circuit, main circuit Mux4x1
module Mux4x1 (
  input  I0,
  input  I1,
  input  I2,
  input  I3,
  input  S1,
  input  S0,
  output Y
);

  wire mux2x1_1_y, mux2x1_2_y;

  Mux2x1 mux2x1_1 (.I0(I0), .I1(I1), .S0(S0), .Y(mux2x1_1_y));
  Mux2x1 mux2x1_2 (.I0(I2), .I1(I3), .S0(S0), .Y(mux2x1_2_y));
  Mux2x1 mux2x1_3 (.I0(mux2x1_1_y), .I1(mux2x1_2_y), .S0(S1), .Y(Y));
endmodule
