// Logisim project ALSU.circ as structural Verilog: 2 circuits, main circuit Bit1_ALSU
module Bit1_ALSU (
  input  Ai,
  input  Bi,
  input  S1,
  input  S0,
  input  Ci,
  input  S2,
  input  S3,
  input  A_prev,
  input  A_next,
  output C_next,
  output out_11
);

  wire and_1_out, and_2_out, and_3_out, and_4_out, bit1_arithmatic_unit_1_di, bit1_logic_unit_1_yi,
       not_1_out, not_2_out;

  Bit1_Arithmatic_Unit bit1_arithmatic_unit_1 (
    .Ai(Ai), .Bi(Bi), .S1(S1), .S0(S0), .Ci(Ci), .Ci1(C_next), .Di(bit1_arithmatic_unit_1_di));
  Bit1_Logic_Unit bit1_logic_unit_1 (.S1(S1), .S0(S0), .Yi(bit1_logic_unit_1_yi));  // open: Ai, Bi
  not not_1 (not_1_out, S2);
  not not_2 (not_2_out, S3);
  and and_1 (and_1_out, bit1_arithmatic_unit_1_di, not_1_out, not_2_out);
  and and_2 (and_2_out, bit1_logic_unit_1_yi, S2, not_2_out);
  and and_3 (and_3_out, A_prev, not_1_out, S3);
  and and_4 (and_4_out, A_next, S2, S3);
  or or_1 (out_11, and_1_out, and_2_out, and_3_out, and_4_out);

  // Notes on the sheet:
  //   ALSU For Moris Mano Machine
  //   ALSU is just a combinational circuit that performs all the provided operations, and the one required is chosen.
  //   Mux 4x1 couldn't be imported here.
endmodule

module ALSU (
  input  S3,
  input  S2,
  input  S0,
  input  S1,
  input  A0,
  input  B0,
  input  C_prev,
  input  A_prev,
  input  A1,
  input  B1,
  input  A2,
  input  B2,
  input  A3,
  input  B3,
  input  A4,
  input  B4,
  input  A5,
  input  B5,
  input  A6,
  input  B6,
  input  A7,
  input  B7,
  input  A8,
  input  B8,
  input  A9,
  input  B9,
  input  A10,
  input  B10,
  input  A11,
  input  B11,
  input  A12,
  input  B12,
  input  A13,
  input  B13,
  input  A14,
  input  B14,
  input  A15,
  input  B15,
  input  A_next,
  output F0,
  output F1,
  output F2,
  output F3,
  output F4,
  output F5,
  output F6,
  output F7,
  output F8,
  output F9,
  output F10,
  output F11,
  output F12,
  output F13,
  output F14,
  output C_next,
  output F15
);

  wire bit1_alsu_1_c_next, bit1_alsu_2_c_next, bit1_alsu_3_c_next, bit1_alsu_4_c_next, bit1_alsu_5_c_next,
       bit1_alsu_6_c_next, bit1_alsu_7_c_next, bit1_alsu_8_c_next, bit1_alsu_9_c_next, bit1_alsu_10_c_next,
       bit1_alsu_11_c_next, bit1_alsu_12_c_next, bit1_alsu_13_c_next, bit1_alsu_14_c_next,
       bit1_alsu_15_c_next;

  Bit1_ALSU bit1_alsu_1 (
    .Ai(A0), .Bi(B0), .S1(S1), .S0(S0), .Ci(C_prev), .S2(S2), .S3(S3), .A_prev(A_prev), .A_next(A1),
    .C_next(bit1_alsu_1_c_next), .out_11(F0));
  Bit1_ALSU bit1_alsu_2 (
    .Ai(A1), .Bi(B1), .S1(S1), .S0(S0), .Ci(bit1_alsu_1_c_next), .S2(S2), .S3(S3), .A_prev(A0), .A_next(A2),
    .C_next(bit1_alsu_2_c_next), .out_11(F1));
  Bit1_ALSU bit1_alsu_3 (
    .Ai(A2), .Bi(B2), .S1(S1), .S0(S0), .Ci(bit1_alsu_2_c_next), .S2(S2), .S3(S3), .A_prev(A1), .A_next(A3),
    .C_next(bit1_alsu_3_c_next), .out_11(F2));
  Bit1_ALSU bit1_alsu_4 (
    .Ai(A3), .Bi(B3), .S1(S1), .S0(S0), .Ci(bit1_alsu_3_c_next), .S2(S2), .S3(S3), .A_prev(A2), .A_next(A4),
    .C_next(bit1_alsu_4_c_next), .out_11(F3));
  Bit1_ALSU bit1_alsu_5 (
    .Ai(A4), .Bi(B4), .S1(S1), .S0(S0), .Ci(bit1_alsu_4_c_next), .S2(S2), .S3(S3), .A_prev(A3), .A_next(A5),
    .C_next(bit1_alsu_5_c_next), .out_11(F4));
  Bit1_ALSU bit1_alsu_6 (
    .Ai(A5), .Bi(B5), .S1(S1), .S0(S0), .Ci(bit1_alsu_5_c_next), .S2(S2), .S3(S3), .A_prev(A4), .A_next(A6),
    .C_next(bit1_alsu_6_c_next), .out_11(F5));
  Bit1_ALSU bit1_alsu_7 (
    .Ai(A6), .Bi(B6), .S1(S1), .S0(S0), .Ci(bit1_alsu_6_c_next), .S2(S2), .S3(S3), .A_prev(A5), .A_next(A7),
    .C_next(bit1_alsu_7_c_next), .out_11(F6));
  Bit1_ALSU bit1_alsu_8 (
    .Ai(A7), .Bi(B7), .S1(S1), .S0(S0), .Ci(bit1_alsu_7_c_next), .S2(S2), .S3(S3), .A_prev(A6), .A_next(A8),
    .C_next(bit1_alsu_8_c_next), .out_11(F7));
  Bit1_ALSU bit1_alsu_9 (
    .Ai(A8), .Bi(B8), .S1(S1), .S0(S0), .Ci(bit1_alsu_8_c_next), .S2(S2), .S3(S3), .A_prev(A7), .A_next(A9),
    .C_next(bit1_alsu_9_c_next), .out_11(F8));
  Bit1_ALSU bit1_alsu_10 (
    .Ai(A9), .Bi(B9), .S1(S1), .S0(S0), .Ci(bit1_alsu_9_c_next), .S2(S2), .S3(S3), .A_prev(A8), .A_next(A10),
    .C_next(bit1_alsu_10_c_next), .out_11(F9));
  Bit1_ALSU bit1_alsu_11 (
    .Ai(A10), .Bi(B10), .S1(S1), .S0(S0), .Ci(bit1_alsu_10_c_next), .S2(S2), .S3(S3), .A_prev(A9),
    .A_next(A11), .C_next(bit1_alsu_11_c_next), .out_11(F10));
  Bit1_ALSU bit1_alsu_12 (
    .Ai(A11), .Bi(B11), .S1(S1), .S0(S0), .Ci(bit1_alsu_11_c_next), .S2(S2), .S3(S3), .A_prev(A10),
    .A_next(A12), .C_next(bit1_alsu_12_c_next), .out_11(F11));
  Bit1_ALSU bit1_alsu_13 (
    .Ai(A12), .Bi(B12), .S1(S1), .S0(S0), .Ci(bit1_alsu_12_c_next), .S2(S2), .S3(S3), .A_prev(A11),
    .A_next(A13), .C_next(bit1_alsu_13_c_next), .out_11(F12));
  Bit1_ALSU bit1_alsu_14 (
    .Ai(A13), .Bi(B13), .S1(S1), .S0(S0), .Ci(bit1_alsu_13_c_next), .S2(S2), .S3(S3), .A_prev(A12),
    .A_next(A14), .C_next(bit1_alsu_14_c_next), .out_11(F13));
  Bit1_ALSU bit1_alsu_15 (
    .Ai(A14), .Bi(B14), .S1(S1), .S0(S0), .Ci(bit1_alsu_14_c_next), .S2(S2), .S3(S3), .A_prev(A13),
    .A_next(A15), .C_next(bit1_alsu_15_c_next), .out_11(F14));
  Bit1_ALSU bit1_alsu_16 (
    .Ai(A15), .Bi(B15), .S1(S1), .S0(S0), .Ci(bit1_alsu_15_c_next), .S2(S2), .S3(S3), .A_prev(A14),
    .A_next(A_next), .C_next(C_next), .out_11(F15));

  // Notes on the sheet:
  //   S2, S3: Define Which one is used out of Arithmetic, Logic and the 2 shifts.
  //   S0, S1: They determine the specific operation inside the Arithmetic and Logic Units.
endmodule
