// Logisim project Arithmetic_Unit.circ as structural Verilog: 2 circuits, main circuit Bit1_Arithmatic_Unit
module Bit1_Arithmatic_Unit (
  input  Ai,
  input  Bi,
  input  S1,
  input  S0,
  input  Ci,
  output Ci1,
  output Di
);

  wire mux4x1_1_y, not_1_out;

  not not_1 (not_1_out, Bi);
  Mux4x1 mux4x1_1 (.I0(Bi), .I1(not_1_out), .I2(1'b0), .I3(1'b1), .S1(S1), .S0(S0), .Y(mux4x1_1_y));
  Full_Adder full_adder_1 (.P(Ai), .Q(mux4x1_1_y), .R(Ci), .C(Ci1), .S(Di));

  // Notes on the sheet:
  //   Di = Ai + Yi + Ci
endmodule

module Arithmetic_Unit (
  input  S1,
  input  S0,
  input  A0,
  input  B0,
  input  Cin,
  input  A1,
  input  B1,
  input  A2,
  input  B2,
  input  A3,
  input  B3,
  output D0,
  output D1,
  output D2,
  output Cout,
  output D3
);

  wire bit1_arithmatic_unit_1_ci1, bit1_arithmatic_unit_2_ci1, bit1_arithmatic_unit_3_ci1;

  Bit1_Arithmatic_Unit bit1_arithmatic_unit_1 (
    .Ai(A0), .Bi(B0), .S1(S1), .S0(S0), .Ci(Cin), .Ci1(bit1_arithmatic_unit_1_ci1), .Di(D0));
  Bit1_Arithmatic_Unit bit1_arithmatic_unit_2 (
    .Ai(A1), .Bi(B1), .S1(S1), .S0(S0), .Ci(bit1_arithmatic_unit_1_ci1), .Ci1(bit1_arithmatic_unit_2_ci1),
    .Di(D1));
  Bit1_Arithmatic_Unit bit1_arithmatic_unit_3 (
    .Ai(A2), .Bi(B2), .S1(S1), .S0(S0), .Ci(bit1_arithmatic_unit_2_ci1), .Ci1(bit1_arithmatic_unit_3_ci1),
    .Di(D2));
  Bit1_Arithmatic_Unit bit1_arithmatic_unit_4 (
    .Ai(A3), .Bi(B3), .S1(S1), .S0(S0), .Ci(bit1_arithmatic_unit_3_ci1), .Ci1(Cout), .Di(D3));

  // Notes on the sheet:
  //   No use for this, for now.
endmodule
