// Logisim project Logic_Unit.circ as structural Verilog: 1 circuit, main circuit Bit16_Logic_Unit
module Bit16_Logic_Unit (
  input  [15:0] A,
  input  [15:0] B,
  input  S0,
  input  S1,
  output [15:0] Yi
);

  wire [15:0] and_1_out, not_1_out, or_1_out, xor_1_out;

  assign and_1_out = A & B;  // AND_Gate and_1, 16 bits wide
  assign or_1_out = A | B;  // OR_Gate or_1, 16 bits wide
  assign xor_1_out = A ^ B;  // XOR_Gate xor_1, 16 bits wide
  assign not_1_out = ~A;  // NOT_Gate not_1, 16 bits wide
  Bit16Mux4x1 bit16mux4x1_1 (
    .I0(and_1_out), .I1(or_1_out), .I2(xor_1_out), .I3(not_1_out), .S0(S0), .S1(S1), .out_7(Yi));
endmodule
