// Logisim project AC.circ as structural Verilog: 1 circuit, main circuit AC_ControlUnit
module AC_ControlUnit (
  input  D0,
  input  D1,
  input  D2,
  input  T5,
  input  p,
  input  r,
  input  B9,
  input  B7,
  input  B6,
  input  B5,
  input  B11,
  input  CLR,
  output ACLD,
  output ACINR,
  output ACCLR
);

  wire and_1_out, and_2_out, and_3_out, and_4_out, and_5_out, and_6_out, and_7_out, and_9_out;

  and and_1 (and_1_out, D0, T5);
  and and_2 (and_2_out, D1, T5);
  and and_3 (and_3_out, D2, T5);
  and and_4 (and_4_out, p, B11);
  and and_5 (and_5_out, r, B9);
  and and_6 (and_6_out, r, B7);
  and and_7 (and_7_out, r, B6);
  and and_8 (ACINR, r, B5);
  and and_9 (and_9_out, r, B11);
  or or_1 (ACLD, and_1_out, and_2_out, and_3_out, and_4_out, and_5_out, and_6_out, and_7_out);
  or or_2 (ACCLR, and_9_out, CLR);

  // Notes on the sheet:
  //   Load = D0T5 + D1T5 +D2T5 + pB11 + rB9 + rB7 + rB6
  //   Increment = rB5
  //   Clear = rB11
endmodule
