// Logisim project AR.circ as structural Verilog: 1 circuit, main circuit main
module main (
  input  [11:0] FromBus,
  input  D7,
  input  I,
  input  T3,
  input  T2,
  input  R,
  input  T0,
  input  D5,
  input  T4
);

  wire and_1_out, and_2_out, and_3_out, and_5_out, not_1_out, not_2_out, or_1_out;

  not not_1 (not_1_out, D7);
  not not_2 (not_2_out, R);
  and and_1 (and_1_out, not_1_out, I, T3);
  and and_2 (and_2_out, T2, not_2_out);
  and and_3 (and_3_out, not_2_out, T0);
  // AND_Gate and_4 has open pins: in0=D5, in1=T4, out=open
  and and_5 (and_5_out, T0, R);
  or or_1 (or_1_out, and_1_out, and_2_out, and_3_out);
  // Bit12_Register bit12_register_1: pin names not known; wires that end beside it: FromBus[0], FromBus[1], FromBus[2], FromBus[3], FromBus[4], FromBus[5], FromBus[6], FromBus[7], FromBus[8], FromBus[9], FromBus[10], FromBus[11], or_1_out, and_5_out
endmodule
