// Logisim project ControlGates.circ as structural Verilog: 3 circuits, main circuit AR
module AR (
  input  [11:0] FromBus,
  input  D7,
  input  I,
  input  T3,
  input  T2,
  input  R,
  input  T0,
  input  D5,
  input  T4,
  input  CLR,
  input  CP,
  output [11:0] ToBus
);

  wire and_1_out, and_2_out, and_3_out, and_4_out, and_5_out, not_1_out, not_2_out, or_1_out, or_2_out;

  not not_1 (not_1_out, D7);
  not not_2 (not_2_out, R);
  and and_1 (and_1_out, not_1_out, I, T3);
  and and_2 (and_2_out, T2, not_2_out);
  and and_3 (and_3_out, not_2_out, T0);
  and and_4 (and_4_out, D5, T4);
  and and_5 (and_5_out, T0, R);
  or or_1 (or_1_out, and_1_out, and_2_out, and_3_out);
  or or_2 (or_2_out, and_5_out, CLR);
  // Bit12_Register AR: pin names not known; wires that end beside it: FromBus, or_1_out, and_4_out, or_2_out, CP, ToBus

  // Notes on the sheet:
  //   Load = R'T0+R'T2+D'7IT3
  //   Increment = D5T4 (BSA)
  //   Clear = RT0
endmodule

module AC (
  input  [15:0] FromBus,
  input  D0,
  input  D1,
  input  D2,
  input  T5,
  input  p,
  input  r,
  input  B9,
  input  B7,
  input  B6,
  input  B5,
  input  B11,
  input  CLR,
  input  CP,
  output [15:0] ToBus
);

  wire and_1_out, and_2_out, and_3_out, and_4_out, and_5_out, and_6_out, and_7_out, and_8_out, and_9_out,
       or_1_out, or_2_out;

  and and_1 (and_1_out, D0, T5);
  and and_2 (and_2_out, D1, T5);
  and and_3 (and_3_out, D2, T5);
  and and_4 (and_4_out, p, B11);
  and and_5 (and_5_out, r, B9);
  and and_6 (and_6_out, r, B7);
  and and_7 (and_7_out, r, B6);
  and and_8 (and_8_out, r, B5);
  and and_9 (and_9_out, r, B11);
  or or_1 (or_1_out, and_1_out, and_2_out, and_3_out, and_4_out, and_5_out, and_6_out, and_7_out);
  or or_2 (or_2_out, and_9_out, CLR);
  // Bit16_Register AC: pin names not known; wires that end beside it: FromBus, or_1_out, and_8_out, or_2_out, CP, ToBus

  // Notes on the sheet:
  //   Load = D0T5 + D1T5 +D2T5 + pB11 + rB9 + rB7 + rB6
  //   Increment = rB5
  //   Clear = rB11
endmodule

module PC (
  input  [15:0] FromBus,
  input  D4,
  input  T4,
  input  D5,
  input  T5,
  input  R,
  input  T1,
  input  in_8,
  input  B11,
  input  B9,
  input  B5,
  input  CLR,
  input  CP,
  output [15:0] ToBus
);

  wire and_1_out, and_2_out, and_3_out, and_4_out, and_5_out, and_6_out, and_7_out, not_1_out, or_1_out,
       or_2_out, or_3_out;

  not not_1 (not_1_out, R);
  and and_1 (and_1_out, D4, T4);
  and and_2 (and_2_out, D5, T5);
  and and_3 (and_3_out, not_1_out, T1);
  and and_4 (and_4_out, in_8, B11);
  and and_5 (and_5_out, in_8, B9);
  and and_6 (and_6_out, in_8, B5);
  and and_7 (and_7_out, R, T1);
  or or_1 (or_1_out, and_1_out, and_2_out);
  or or_2 (or_2_out, and_3_out, and_4_out, and_5_out, and_6_out);
  or or_3 (or_3_out, and_7_out, CLR);
  // Bit16_Register PC: pin names not known; wires that end beside it: FromBus, or_1_out, or_2_out, or_3_out, CP, ToBus

  // Notes on the sheet:
  //   Load = D4T4 + D5T5
  //   BUN & BSA
  //   Fetch & Skip Instructions
  //   Increment = R'T1 + rB11 + rB9 + rB5
  //   Clear = RT1
endmodule
