// Logisim project DR.circ as structural Verilog: 1 circuit, main circuit DR_ControlUnit
module DR_ControlUnit (
  input  D0,
  input  D1,
  input  D2,
  input  D6,
  input  T4,
  input  T5,
  input  CLR,
  output DRLD,
  output DRINC,
  output DRCLR
);

  wire or_1_out;

  or or_1 (or_1_out, D0, D1, D2, D6);
  and and_1 (DRLD, or_1_out, T4);
  and and_2 (DRINC, D6, T5);

  assign DRCLR = CLR;

  // Notes on the sheet:
  //   ISZ
  //   Read Operand
endmodule
