// Logisim project E.circ as structural Verilog: 1 circuit, main circuit E_ControlUnit
module E_ControlUnit (
  input  D1,
  input  T5,
  input  r,
  input  B7,
  input  B6,
  input  B10,
  input  B8,
  output ELD,
  output ECLR,
  output ECMP
);

  wire and_1_out, and_2_out, and_3_out;

  and and_1 (and_1_out, D1, T5);
  and and_2 (and_2_out, r, B7);
  and and_3 (and_3_out, r, B6);
  and and_4 (ECLR, r, B10);
  and and_5 (ECMP, r, B8);
  or or_1 (ELD, and_1_out, and_2_out, and_3_out);
endmodule
