// Logisim project EnableFFs.circ as structural Verilog: 2 circuits, main circuit EnableControlUnitWrong
module EnableControlUnitWrong (
  input  T2,
  input  D4,
  input  T4,
  input  T0,
  input  D5,
  input  D0,
  input  T5,
  input  D1,
  input  D2,
  input  D6,
  input  T6,
  input  D3,
  input  D7,
  input  T3,
  input  B11,
  input  R,
  input  T1,
  input  I,
  output EAR,
  output EPC,
  output EDR,
  output EAC,
  output EIR,
  output ETR,
  output EMEM
);

  wire and_1_out, and_3_out, and_4_out, and_5_out, and_6_out, and_7_out, and_8_out, and_9_out, and_10_out,
       and_11_out, and_12_out, not_1_out, or_1_out;

  not not_1 (not_1_out, D7);
  and and_1 (and_1_out, not_1_out, I, T3);
  or or_1 (or_1_out, D0, D1, D6, D2);
  and and_2 (EAR, D4, T4);
  and and_3 (and_3_out, D5, T4);
  and and_4 (and_4_out, D0, T5);
  and and_5 (and_5_out, D1, T5);
  and and_6 (and_6_out, D2, T5);
  and and_7 (and_7_out, D6, T6);
  and and_8 (and_8_out, D3, T4);
  and and_9 (and_9_out, D7, T3, B11);
  and and_10 (and_10_out, R, T2);
  and and_11 (and_11_out, R, T1);
  and and_12 (and_12_out, T4, or_1_out);
  or or_2 (EPC, T0, and_3_out);
  or or_3 (EDR, and_4_out, and_5_out, and_6_out, and_7_out);
  or or_4 (EAC, and_8_out, and_9_out);
  or or_5 (ETR, and_10_out, and_11_out);
  or or_6 (EMEM, T1, and_1_out, and_12_out);

  assign EIR = T2;
endmodule

module Enable_ControlUnit (
  input  T2,
  input  D4,
  input  T4,
  input  T0,
  input  D5,
  input  D0,
  input  T5,
  input  D1,
  input  D2,
  input  D6,
  input  T6,
  input  D3,
  input  p,
  input  B10,
  input  s_r,
  input  B9,
  input  B7,
  input  B6,
  input  R,
  input  T1,
  output EAR,
  output EPC,
  output EDR,
  output EAC,
  output EIR,
  output ETR
);

  wire and_1_out, and_2_out, and_3_out, and_4_out, and_5_out, and_6_out, and_7_out, and_8_out, and_9_out,
       and_10_out, not_1_out, or_1_out;

  and and_1 (and_1_out, p, B10);
  or or_1 (or_1_out, B9, B7, B6);
  not not_1 (not_1_out, R);
  and and_2 (and_2_out, D4, T4);
  and and_3 (and_3_out, D5, T5);
  and and_4 (and_4_out, D5, T4);
  and and_5 (and_5_out, D0, T5);
  and and_6 (and_6_out, D1, T5);
  and and_7 (and_7_out, D2, T5);
  and and_8 (and_8_out, D6, T6);
  and and_9 (and_9_out, D3, T4);
  and and_10 (and_10_out, s_r, or_1_out);
  and and_11 (EIR, T2, not_1_out);
  and and_12 (ETR, R, T1);
  or or_2 (EAR, and_2_out, and_3_out);
  or or_3 (EPC, T0, and_4_out);
  or or_4 (EDR, and_5_out, and_6_out, and_7_out, and_8_out);
  or or_5 (EAC, and_9_out, and_1_out, and_10_out);
endmodule
