// Logisim project IO.circ as structural Verilog: 1 circuit, main circuit IO
module IO (
  input  p,
  input  B7,
  input  R,
  input  T2,
  input  B6,
  input  s_r,
  input  B0,
  input  T0,
  input  T1,
  input  IEN,
  input  FGI,
  input  FGO,
  input  B11,
  input  B10,
  output IENSET,
  output IENCLR,
  output SCLR,
  output RSET,
  output RCLR,
  output FGICLR,
  output FGOCLR,
  output CPE
);

  wire and_1_out, and_2_out, not_1_out, not_2_out, not_3_out, or_1_out;

  not not_1 (not_1_out, T0);
  not not_2 (not_2_out, T1);
  or or_1 (or_1_out, FGI, FGO);
  not not_3 (not_3_out, T2);
  and and_1 (and_1_out, R, T2);
  and and_2 (and_2_out, p, B6);
  and and_3 (IENSET, p, B7);
  or or_2 (IENCLR, and_1_out, and_2_out);
  and and_4 (SCLR, s_r, B0);
  and and_5 (RSET, not_1_out, not_2_out, IEN, not_3_out, or_1_out);
  and and_6 (RCLR, R, T2);
  and and_7 (FGICLR, p, B11);
  and and_8 (FGOCLR, p, B10);
  not not_4 (CPE, SCLR);
endmodule
