// Logisim project IR.circ as structural Verilog: 1 circuit, main circuit IR_ControlUnit
module IR_ControlUnit (
  input  R,
  input  T1,
  input  CLR,
  output IRLD,
  output IRCLR
);

  wire not_1_out;

  not not_1 (not_1_out, R);
  and and_1 (IRLD, not_1_out, T1);

  assign IRCLR = CLR;
endmodule
