// Logisim project Mem.circ as structural Verilog: 1 circuit, main circuit Mem_ControlUnit
module Mem_ControlUnit (
  input  D7,
  input  I,
  input  T3,
  input  R,
  input  T1,
  input  D0,
  input  D1,
  input  D2,
  input  D6,
  input  T4,
  input  T6,
  input  D5,
  input  D3,
  output READ,
  output WRITE
);

  wire and_1_out, and_2_out, and_3_out, and_4_out, and_5_out, and_6_out, and_7_out, not_1_out, not_2_out,
       or_1_out;

  not not_1 (not_1_out, D7);
  not not_2 (not_2_out, R);
  and and_1 (and_1_out, not_1_out, I, T3);
  and and_2 (and_2_out, not_2_out, T1);
  or or_1 (or_1_out, D0, D1, D2, D6);
  and and_3 (and_3_out, or_1_out, T4);
  and and_4 (and_4_out, D6, T6);
  and and_5 (and_5_out, T4, D5);
  and and_6 (and_6_out, T4, D3);
  and and_7 (and_7_out, R, T1);
  or or_2 (READ, and_1_out, and_2_out, and_3_out);
  or or_3 (WRITE, and_4_out, and_5_out, and_6_out, and_7_out);
endmodule
