// Logisim project PC.circ as structural Verilog: 1 circuit, main circuit PC_ControlUnit
module PC_ControlUnit (
  input  D4,
  input  T4,
  input  D5,
  input  T5,
  input  R,
  input  T1,
  input  T2,
  input  B4,
  input  AC_15,
  input  B3,
  input  AC_equals_0,
  input  B2,
  input  E_equals_0,
  input  B1,
  input  s_r,
  input  p,
  input  B9,
  input  FGI,
  input  B8,
  input  FGO,
  input  D6,
  input  T6,
  input  DR_equals_0,
  input  CLR,
  output PCLD,
  output PCINR,
  output PCCLR
);

  wire and_1_out, and_2_out, and_3_out, and_4_out, and_5_out, and_6_out, and_7_out, and_8_out, and_9_out,
       and_10_out, and_11_out, and_12_out, not_1_out, not_2_out;

  not not_1 (not_1_out, R);
  not not_2 (not_2_out, AC_15);
  and and_1 (and_1_out, D4, T4);
  and and_2 (and_2_out, D5, T5);
  and and_3 (and_3_out, not_1_out, T1);
  and and_4 (and_4_out, R, T2);
  and and_5 (and_5_out, B4, not_2_out, s_r);
  and and_6 (and_6_out, AC_15, B3, s_r);
  and and_7 (and_7_out, AC_equals_0, B2, s_r);
  and and_8 (and_8_out, E_equals_0, B1, s_r);
  and and_9 (and_9_out, p, B9, FGI);
  and and_10 (and_10_out, p, B8, FGO);
  and and_11 (and_11_out, D6, T6, DR_equals_0);
  and and_12 (and_12_out, R, T1);
  or or_1 (PCLD, and_1_out, and_2_out);
  or or_2 (PCINR, and_4_out, and_5_out, and_3_out, and_6_out, and_7_out, and_8_out, and_9_out, and_10_out, and_11_out);
  or or_3 (PCCLR, and_12_out, CLR);

  // Notes on the sheet:
  //   BUN & BSA
  //   Load = D4T4 + D5T5
  //   Increment = R'T1 + rB11 + rB9 + rB5
  //   Fetch & Skip Instructions
  //   Clear = RT1
endmodule
