// Logisim project Registers.circ as structural Verilog: 5 circuits, main circuit Bit8_Register
module Bit8_Register (
  input  I0,
  input  I1,
  input  I2,
  input  I3,
  input  I4,
  input  I5,
  input  I6,
  input  I7,
  input  Load,
  input  CP,
  input  CLR,
  input  INR,
  output A0,
  output A1,
  output A2,
  output A3,
  output A4,
  output A5,
  output A6,
  output A7,
  output C
);

  wire bit4_register_1_c;

  Bit4_Register bit4_register_1 (
    .I0(I0), .I1(I1), .I2(I2), .I3(I3), .LD(Load), .CP(CP), .CLR(CLR), .INR(INR), .A0(A0), .A1(A1), .A2(A2),
    .A3(A3), .C(bit4_register_1_c));
  Bit4_Register bit4_register_2 (
    .I0(I4), .I1(I5), .I2(I6), .I3(I7), .LD(Load), .CP(CP), .CLR(CLR), .INR(bit4_register_1_c), .A0(A4),
    .A1(A5), .A2(A6), .A3(A7), .C(C));
endmodule

module Bit12_Register (
  input  I0,
  input  I1,
  input  I2,
  input  I3,
  input  I4,
  input  I5,
  input  I6,
  input  I7,
  input  I8,
  input  I9,
  input  I10,
  input  I11,
  input  Load,
  input  CP,
  input  CLR,
  input  INR,
  output A0,
  output A1,
  output A2,
  output A3,
  output A4,
  output A5,
  output A6,
  output A7,
  output A8,
  output A9,
  output A10,
  output A11,
  output C
);

  wire bit4_register_1_c, bit4_register_2_p13;

  Bit4_Register bit4_register_1 (
    .I0(I0), .I1(I1), .I2(I2), .I3(I3), .LD(Load), .CP(CP), .CLR(CLR), .INR(INR), .A0(A0), .A1(A1), .A2(A2),
    .A3(A3), .C(bit4_register_1_c));
  // Bit4_Register bit4_register_2: pin names not known; wires that end beside it: I4, I5, I6, I7, Load, CP, CLR, bit4_register_1_c, A7, A4, A5, A6, bit4_register_2_p13
  Bit4_Register bit4_register_3 (
    .I0(I8), .I1(I9), .I2(I10), .I3(I11), .LD(Load), .CP(CP), .CLR(CLR), .INR(bit4_register_2_p13), .A0(A8),
    .A1(A9), .A2(A10), .A3(A11), .C(C));
endmodule

module Bit16_Register (
  input  I0,
  input  I1,
  input  I2,
  input  I3,
  input  I4,
  input  I5,
  input  I6,
  input  I7,
  input  I8,
  input  I9,
  input  I10,
  input  I11,
  input  I12,
  input  I13,
  input  I14,
  input  I15,
  input  Load,
  input  CP,
  input  CLR,
  input  INR,
  output A0,
  output A1,
  output A2,
  output A3,
  output A4,
  output A5,
  output A6,
  output A7,
  output A8,
  output A9,
  output A10,
  output A11,
  output A12,
  output A13,
  output A14,
  output A15,
  output C
);

  wire bit4_register_1_c, bit4_register_2_c, bit4_register_3_c;

  Bit4_Register bit4_register_1 (
    .I0(I0), .I1(I1), .I2(I2), .I3(I3), .LD(Load), .CP(CP), .CLR(CLR), .INR(INR), .A0(A0), .A1(A1), .A2(A2),
    .A3(A3), .C(bit4_register_1_c));
  Bit4_Register bit4_register_2 (
    .I0(I4), .I1(I5), .I2(I6), .I3(I7), .LD(Load), .CP(CP), .CLR(CLR), .INR(bit4_register_1_c), .A0(A4),
    .A1(A5), .A2(A6), .A3(A7), .C(bit4_register_2_c));
  Bit4_Register bit4_register_3 (
    .I0(I8), .I1(I9), .I2(I10), .I3(I11), .LD(Load), .CP(CP), .CLR(CLR), .INR(bit4_register_2_c), .A0(A8),
    .A1(A9), .A2(A10), .A3(A11), .C(bit4_register_3_c));
  Bit4_Register bit4_register_4 (
    .I0(I12), .I1(I13), .I2(I14), .I3(I15), .LD(Load), .CP(CP), .CLR(CLR), .INR(bit4_register_3_c), .A0(A12),
    .A1(A13), .A2(A14), .A3(A15), .C(C));
endmodule

module Bit4_Register (
  input  I0,
  input  I1,
  input  I2,
  input  I3,
  input  LD,
  input  CP,
  input  CLR,
  input  INR,
  output A0,
  output A1,
  output A2,
  output A3,
  output C
);

  wire and_1_out, and_2_out, and_3_out, and_4_out, and_5_out, and_6_out, and_7_out, and_8_out, and_9_out,
       and_10_out, and_11_out, and_12_out, and_13_out, not_1_out, not_2_out, not_3_out, not_4_out, not_5_out,
       not_6_out, or_1_out, or_2_out, or_3_out, or_4_out, or_5_out, or_6_out, or_7_out, or_8_out;

  not not_1 (not_1_out, I0);
  not not_2 (not_2_out, I1);
  not not_3 (not_3_out, I2);
  not not_4 (not_4_out, I3);
  not not_5 (not_5_out, CLR);
  not not_6 (not_6_out, LD);
  and and_1 (and_1_out, LD, not_5_out);
  and and_2 (and_2_out, and_1_out, I0);
  and and_3 (and_3_out, and_1_out, not_1_out);
  and and_4 (and_4_out, and_1_out, I1);
  and and_5 (and_5_out, and_1_out, not_2_out);
  and and_6 (and_6_out, and_1_out, I2);
  and and_7 (and_7_out, and_1_out, not_3_out);
  and and_8 (and_8_out, and_1_out, I3);
  and and_9 (and_9_out, and_1_out, not_4_out);
  and and_10 (and_10_out, not_6_out, INR, not_5_out);
  and and_11 (and_11_out, and_10_out, A0);
  and and_12 (and_12_out, and_11_out, A1);
  and and_13 (and_13_out, and_12_out, A2);
  and and_14 (C, and_13_out, A3);
  or or_1 (or_1_out, and_10_out, and_2_out);
  or or_2 (or_2_out, and_3_out, and_10_out);
  or or_3 (or_3_out, and_11_out, and_4_out);
  or or_4 (or_4_out, and_5_out, and_11_out);
  or or_5 (or_5_out, and_12_out, and_6_out);
  or or_6 (or_6_out, and_7_out, and_12_out);
  or or_7 (or_7_out, and_13_out, and_8_out);
  or or_8 (or_8_out, and_9_out, and_13_out);
  // Master_Slave_Flip_Flop master_slave_flip_flop_1: pin names not known; wires that end beside it: or_1_out, CP, or_2_out, CLR, A0
  // Master_Slave_Flip_Flop master_slave_flip_flop_2: pin names not known; wires that end beside it: or_3_out, CP, or_4_out, CLR, A1
  // Master_Slave_Flip_Flop master_slave_flip_flop_3: pin names not known; wires that end beside it: or_5_out, CP, or_6_out, CLR, A2
  // Master_Slave_Flip_Flop master_slave_flip_flop_4: pin names not known; wires that end beside it: or_7_out, CP, or_8_out, CLR, A3
endmodule

module test (
  input  in_1,
  input  in_2,
  input  in_3
);

  wire clock_1_out, master_slave_flip_flop_1_p5, master_slave_flip_flop_1_p6;

  Clock clock_1 (.out(clock_1_out));
  // Master_Slave_Flip_Flop master_slave_flip_flop_1: pin names not known; wires that end beside it: in_1, clock_1_out, in_2, in_3, master_slave_flip_flop_1_p5, master_slave_flip_flop_1_p6
endmodule
