// Logisim project SC.circ as structural Verilog: 1 circuit, main circuit SC_ControlUnit
module SC_ControlUnit (
  input  R,
  input  T2,
  input  s_r,
  input  p,
  input  D6,
  input  T6,
  input  T4,
  input  D3,
  input  D4,
  input  T5,
  input  D0,
  input  D1,
  input  D2,
  input  D5,
  input  CLR,
  output SCCLR
);

  wire and_1_out, and_2_out, and_3_out, and_4_out, or_1_out, or_2_out, or_3_out, or_4_out;

  or or_1 (or_1_out, D3, D4);
  or or_2 (or_2_out, D0, D1, D2, D5);
  and and_1 (and_1_out, R, T2);
  or or_3 (or_3_out, s_r, p);
  and and_2 (and_2_out, D6, T6);
  and and_3 (and_3_out, T4, or_1_out);
  and and_4 (and_4_out, T5, or_2_out);
  or or_4 (or_4_out, and_1_out, or_3_out, and_2_out, and_3_out, and_4_out);
  or or_5 (SCCLR, or_4_out, CLR);
endmodule
