// Logisim project TR.circ as structural Verilog: 1 circuit, main circuit TR_ControlUnit
module TR_ControlUnit (
  input  R,
  input  T0,
  input  CLR,
  output TRLD,
  output TRINR,
  output TRCLR
);

  and and_1 (TRLD, R, T0);

  assign TRCLR = CLR;
  assign TRINR = 1'b0;
endmodule
