// Logisim project BasicComputer.circ as structural Verilog: 3 circuits, main circuit CompleteComputer
module CompleteComputer (
);

  wire and_1_out, bit16_alsu_1_c_next, control_unit_1_p3, control_unit_1_p5, control_unit_1_p7,
       control_unit_1_p8, control_unit_1_p9, control_unit_1_p10, control_unit_1_p11, control_unit_1_p13,
       control_unit_1_p14, control_unit_1_p15, control_unit_1_p16, control_unit_1_p17, control_unit_1_p18,
       control_unit_1_p20, control_unit_1_p22, control_unit_1_p23, control_unit_1_p24, control_unit_1_p25,
       control_unit_1_p26, control_unit_1_p27, control_unit_1_p28, control_unit_1_p29, control_unit_1_p30,
       control_unit_1_p31, control_unit_1_p32, control_unit_1_p33, control_unit_1_p34, control_unit_1_p35,
       control_unit_1_p36, control_unit_1_p37, control_unit_1_p38, control_unit_1_p39, control_unit_1_p40,
       control_unit_1_p41, control_unit_1_p42, control_unit_1_p43, control_unit_1_p44, control_unit_1_p45,
       control_unit_1_p46, control_unit_1_p47, control_unit_1_p48, control_unit_1_p49, CP_out, FGO_p5,
       keyboard_1_avail, Reset_out, S_p5, S_p6;
  wire [3:0] control_unit_1_p1, control_unit_1_p2, control_unit_1_p2_2, control_unit_1_p2_3,
       control_unit_1_p2_4, control_unit_1_p4, control_unit_1_p4_2, control_unit_1_p4_3, control_unit_1_p4_4,
       control_unit_1_p6, control_unit_1_p6_2, control_unit_1_p6_3, control_unit_1_p6_4,
       controlled_buffer_1_out, controlled_buffer_1_out_2, controlled_buffer_1_out_3,
       controlled_buffer_3_out, SC_a0;
  wire [6:0] keyboard_1_data;
  wire [7:0] INPR_a, OUTR_a;
  wire [11:0] AR_a, PC_a;
  wire [15:0] bit16_alsu_1_f, multiplexer_1_out, ram_1_dout, TR_a;

  Clock CP (.out(CP_out));
  Multiplexer #(.width(16)) multiplexer_1 (
    .in0({control_unit_1_p4_4, control_unit_1_p4_3, control_unit_1_p4_2, control_unit_1_p4}),
    .in1({{8{1'b0}}, INPR_a}), .out(multiplexer_1_out), .sel(control_unit_1_p48));
  and and_1 (and_1_out, S_p6, CP_out);
  Button Reset (.out(Reset_out));
  Bit4_Counter SC (
    .INR(1'b1), .CP(and_1_out), .CLR(control_unit_1_p5), .A0(SC_a0[0]), .A1(SC_a0[1]), .A2(SC_a0[2]),
    .A3(SC_a0[3]));
  Hex_Digit_Display hex_digit_display_1 (.value(control_unit_1_p1));  // open: dp
  // Control_Unit control_unit_1: pin names not known; wires that end beside it: control_unit_1_p1, {control_unit_1_p2_4, control_unit_1_p2_3, control_unit_1_p2_2, control_unit_1_p2}, control_unit_1_p3, {control_unit_1_p4_4, control_unit_1_p4_3, control_unit_1_p4_2, control_unit_1_p4}, control_unit_1_p5, {control_unit_1_p6_4, control_unit_1_p6_3, control_unit_1_p6_2, control_unit_1_p6}, control_unit_1_p7, control_unit_1_p8, control_unit_1_p9, control_unit_1_p10, control_unit_1_p11, 1'b0, control_unit_1_p13, control_unit_1_p14, control_unit_1_p15, control_unit_1_p16, control_unit_1_p17, control_unit_1_p18, SC_a0, control_unit_1_p20, Reset_out, control_unit_1_p22, control_unit_1_p23, control_unit_1_p24, control_unit_1_p25, control_unit_1_p26, control_unit_1_p27, control_unit_1_p28, control_unit_1_p29, control_unit_1_p30, control_unit_1_p31, control_unit_1_p32, control_unit_1_p33, control_unit_1_p34, control_unit_1_p35, control_unit_1_p36, control_unit_1_p37, control_unit_1_p38, control_unit_1_p39, control_unit_1_p40, control_unit_1_p41, control_unit_1_p42, control_unit_1_p43, control_unit_1_p44, control_unit_1_p45, control_unit_1_p46, control_unit_1_p47, control_unit_1_p48, control_unit_1_p49
  Hex_Digit_Display hex_digit_display_2 (.value(SC_a0));  // open: dp
  Bit16_ALSU bit16_alsu_1 (
    .A(multiplexer_1_out),
    .B({control_unit_1_p6_4, control_unit_1_p6_3, control_unit_1_p6_2, control_unit_1_p6}),
    .S(control_unit_1_p1), .C_prev(control_unit_1_p3), .F(bit16_alsu_1_f), .C_next(bit16_alsu_1_c_next));
  Keyboard #(.buflen(8)) keyboard_1 (
    .clk(and_1_out), .re(control_unit_1_p48), .clr(Reset_out), .avail(keyboard_1_avail),
    .data(keyboard_1_data));
  RAM #(.addrWidth(12), .asyncread("true"), .dataWidth(16)) ram_1 (
    .addr(AR_a), .we(control_unit_1_p27), .oe(control_unit_1_p26), .clk(and_1_out),
    .din({controlled_buffer_3_out, controlled_buffer_1_out_3, controlled_buffer_1_out_2, controlled_buffer_1_out}),
    .dout(ram_1_dout));
  Bit12_Register AR (
    .I({controlled_buffer_1_out_3, controlled_buffer_1_out_2, controlled_buffer_1_out}),
    .Load(control_unit_1_p14), .INR(control_unit_1_p16), .CLR(control_unit_1_p18), .CP(and_1_out), .A(AR_a));  // open: C
  Hex_Digit_Display hex_digit_display_3 (.value(AR_a[11:8]));  // open: dp
  Bit12_Register PC (
    .I({controlled_buffer_1_out_3, controlled_buffer_1_out_2, controlled_buffer_1_out}),
    .Load(control_unit_1_p28), .INR(control_unit_1_p29), .CLR(control_unit_1_p30), .CP(and_1_out), .A(PC_a));  // open: C
  Hex_Digit_Display hex_digit_display_4 (.value(PC_a[11:8]));  // open: dp
  Bit16_Register DR (
    .I({controlled_buffer_3_out, controlled_buffer_1_out_3, controlled_buffer_1_out_2, controlled_buffer_1_out}),
    .Load(control_unit_1_p20), .INR(control_unit_1_p22), .CLR(control_unit_1_p23), .CP(and_1_out),
    .A({control_unit_1_p4_4, control_unit_1_p4_3, control_unit_1_p4_2, control_unit_1_p4}));  // open: C
  Hex_Digit_Display hex_digit_display_5 (.value(control_unit_1_p4_4));  // open: dp
  Bit16_Register AC (
    .I(bit16_alsu_1_f), .Load(control_unit_1_p7), .INR(control_unit_1_p9), .CLR(control_unit_1_p11),
    .CP(and_1_out), .A({control_unit_1_p6_4, control_unit_1_p6_3, control_unit_1_p6_2, control_unit_1_p6}));  // open: C
  Hex_Digit_Display hex_digit_display_6 (.value(control_unit_1_p6_4));  // open: dp
  Bit8_Register INPR (
    .I({1'b0, keyboard_1_data}), .Load(keyboard_1_avail), .INR(1'b0), .CLR(Reset_out), .CP(and_1_out),
    .A(INPR_a));  // open: C
  Hex_Digit_Display hex_digit_display_7 (.value(INPR_a[7:4]));  // open: dp
  Bit16_Register IR (
    .I({controlled_buffer_3_out, controlled_buffer_1_out_3, controlled_buffer_1_out_2, controlled_buffer_1_out}),
    .Load(control_unit_1_p24), .INR(1'b0), .CLR(control_unit_1_p25), .CP(and_1_out),
    .A({control_unit_1_p2_4, control_unit_1_p2_3, control_unit_1_p2_2, control_unit_1_p2}));  // open: C
  Hex_Digit_Display hex_digit_display_8 (.value(control_unit_1_p2_4));  // open: dp
  Bit16_Register TR (
    .I({controlled_buffer_3_out, controlled_buffer_1_out_3, controlled_buffer_1_out_2, controlled_buffer_1_out}),
    .Load(control_unit_1_p31), .INR(control_unit_1_p32), .CLR(control_unit_1_p33), .CP(and_1_out), .A(TR_a));  // open: C
  Hex_Digit_Display hex_digit_display_9 (.value(TR_a[15:12]));  // open: dp
  Bit8_Register OUTR (
    .I({controlled_buffer_1_out_2, controlled_buffer_1_out}), .Load(control_unit_1_p49), .INR(1'b0),
    .CLR(Reset_out), .CP(and_1_out), .A(OUTR_a));  // open: C
  // Master_Slave_Flip_Flop IEN: pin names not known; wires that end beside it: control_unit_1_p44, and_1_out, control_unit_1_p43, Reset_out, control_unit_1_p13
  // Master_Slave_Flip_Flop S: pin names not known; wires that end beside it: control_unit_1_p45, and_1_out, Reset_out, Reset_out, S_p5, S_p6
  // Master_Slave_Flip_Flop R: pin names not known; wires that end beside it: control_unit_1_p46, and_1_out, control_unit_1_p47, Reset_out, control_unit_1_p8
  // Master_Slave_Flip_Flop FGI: pin names not known; wires that end beside it: keyboard_1_avail, and_1_out, control_unit_1_p48, Reset_out, control_unit_1_p15
  // Master_Slave_Flip_Flop FGO: pin names not known; wires that end beside it: control_unit_1_p49, and_1_out, 1'b1, Reset_out, FGO_p5, control_unit_1_p17
  E_Register E (
    .ELD(control_unit_1_p40), .ALU_E(bit16_alsu_1_c_next), .ECMP(control_unit_1_p42),
    .ECLR(control_unit_1_p41), .CP(and_1_out), .Reset(Reset_out), .E(control_unit_1_p10));
  Hex_Digit_Display hex_digit_display_10 (.value(ram_1_dout[15:12]));  // open: dp
  Hex_Digit_Display hex_digit_display_11 (.value(ram_1_dout[11:8]));  // open: dp
  Hex_Digit_Display hex_digit_display_12 (.value(AR_a[7:4]));  // open: dp
  Hex_Digit_Display hex_digit_display_13 (.value(AR_a[3:0]));  // open: dp
  Hex_Digit_Display hex_digit_display_14 (.value(PC_a[7:4]));  // open: dp
  Hex_Digit_Display hex_digit_display_15 (.value(PC_a[3:0]));  // open: dp
  Hex_Digit_Display hex_digit_display_16 (.value(control_unit_1_p4_3));  // open: dp
  Hex_Digit_Display hex_digit_display_17 (.value(control_unit_1_p4_2));  // open: dp
  Hex_Digit_Display hex_digit_display_18 (.value(control_unit_1_p6_3));  // open: dp
  Hex_Digit_Display hex_digit_display_19 (.value(control_unit_1_p6_2));  // open: dp
  Hex_Digit_Display hex_digit_display_20 (.value(INPR_a[3:0]));  // open: dp
  Hex_Digit_Display hex_digit_display_21 (.value(control_unit_1_p2_3));  // open: dp
  Hex_Digit_Display hex_digit_display_22 (.value(control_unit_1_p2_2));  // open: dp
  Hex_Digit_Display hex_digit_display_23 (.value(TR_a[11:8]));  // open: dp
  Hex_Digit_Display hex_digit_display_24 (.value(TR_a[7:4]));  // open: dp
  TTY #(.cols(8)) tty_1 (.data(OUTR_a[6:0]), .clk(and_1_out), .we(FGO_p5), .clr(Reset_out));
  LED Done (.in(S_p5));
  Hex_Digit_Display hex_digit_display_25 (.value(ram_1_dout[7:4]));  // open: dp
  Hex_Digit_Display hex_digit_display_26 (.value(ram_1_dout[3:0]));  // open: dp
  Hex_Digit_Display hex_digit_display_27 (.value(control_unit_1_p4));  // open: dp
  Hex_Digit_Display hex_digit_display_28 (.value(control_unit_1_p6));  // open: dp
  Hex_Digit_Display hex_digit_display_29 (.value(control_unit_1_p2));  // open: dp
  Hex_Digit_Display hex_digit_display_30 (.value(TR_a[3:0]));  // open: dp
  assign {controlled_buffer_1_out_3, controlled_buffer_1_out_2, controlled_buffer_1_out} = control_unit_1_p34 ? AR_a : 12'bz;  // Controlled_Buffer controlled_buffer_1
  assign {controlled_buffer_1_out_3, controlled_buffer_1_out_2, controlled_buffer_1_out} = control_unit_1_p35 ? PC_a : 12'bz;  // Controlled_Buffer controlled_buffer_2
  assign {controlled_buffer_3_out, controlled_buffer_1_out_3, controlled_buffer_1_out_2, controlled_buffer_1_out} = control_unit_1_p36 ? {control_unit_1_p4_4, control_unit_1_p4_3, control_unit_1_p4_2, control_unit_1_p4} : 16'bz;  // Controlled_Buffer controlled_buffer_3
  Hex_Digit_Display hex_digit_display_31 (.value(controlled_buffer_3_out));  // open: dp
  Hex_Digit_Display hex_digit_display_32 (.value(controlled_buffer_1_out_3));  // open: dp
  assign {controlled_buffer_3_out, controlled_buffer_1_out_3, controlled_buffer_1_out_2, controlled_buffer_1_out} = control_unit_1_p37 ? {control_unit_1_p6_4, control_unit_1_p6_3, control_unit_1_p6_2, control_unit_1_p6} : 16'bz;  // Controlled_Buffer controlled_buffer_4
  Hex_Digit_Display hex_digit_display_33 (.value(controlled_buffer_1_out_2));  // open: dp
  Hex_Digit_Display hex_digit_display_34 (.value(controlled_buffer_1_out));  // open: dp
  assign {controlled_buffer_3_out, controlled_buffer_1_out_3, controlled_buffer_1_out_2, controlled_buffer_1_out} = control_unit_1_p38 ? {control_unit_1_p2_4, control_unit_1_p2_3, control_unit_1_p2_2, control_unit_1_p2} : 16'bz;  // Controlled_Buffer controlled_buffer_5
  assign {controlled_buffer_3_out, controlled_buffer_1_out_3, controlled_buffer_1_out_2, controlled_buffer_1_out} = control_unit_1_p26 ? ram_1_dout : 16'bz;  // Controlled_Buffer controlled_buffer_6
  assign {controlled_buffer_3_out, controlled_buffer_1_out_3, controlled_buffer_1_out_2, controlled_buffer_1_out} = control_unit_1_p39 ? TR_a : 16'bz;  // Controlled_Buffer controlled_buffer_7
endmodule

module E_Register (
  input  ELD,
  input  ALU_E,
  input  ECMP,
  input  ECLR,
  input  CP,
  input  Reset,
  output E
);

  wire and_1_out, and_2_out, not_1_out, or_1_out, or_2_out;

  and and_1 (and_1_out, ELD, ALU_E);
  and and_2 (and_2_out, ELD, not_1_out);
  not not_1 (not_1_out, ALU_E);
  or or_1 (or_1_out, and_1_out, ECMP);
  or or_2 (or_2_out, ECMP, and_2_out, ECLR);
  // Master_Slave_Flip_Flop FGO: pin names not known; wires that end beside it: or_1_out, CP, or_2_out, Reset, E
endmodule

module test (
  input  in_1,
  input  in_2,
  input  in_3,
  output out_4
);

  wire clock_1_out;
  wire [6:0] keyboard_1_data;

  Clock clock_1 (.out(clock_1_out));
  Keyboard #(.buflen(8)) keyboard_1 (.clk(clock_1_out), .re(in_1), .clr(in_2), .avail(out_4), .data(keyboard_1_data));
  Hex_Digit_Display hex_digit_display_1 (.value(keyboard_1_data[3:0]));  // open: dp
  Hex_Digit_Display hex_digit_display_2 (.value({in_3, keyboard_1_data[6:4]}));  // open: dp
endmodule
