// Logisim project Registers.circ as structural Verilog: 4 circuits, main circuit Bit8_Register
module Bit8_Register (
  input  [7:0] I,
  input  Load,
  input  INR,
  input  CLR,
  input  CP,
  input  Reset,
  output [7:0] A,
  output C
);

  wire bit4_register_1_c;

  Bit4_Register bit4_register_1 (
    .I0(I[0]), .I1(I[1]), .I2(I[2]), .I3(I[3]), .LD(Load), .CP(CP), .CLR(CLR), .INR(INR), .Reset(Reset),
    .A0(A[0]), .A1(A[1]), .A2(A[2]), .A3(A[3]), .C(bit4_register_1_c));
  Bit4_Register bit4_register_2 (
    .I0(I[4]), .I1(I[5]), .I2(I[6]), .I3(I[7]), .LD(Load), .CP(CP), .CLR(CLR), .INR(bit4_register_1_c),
    .Reset(Reset), .A0(A[4]), .A1(A[5]), .A2(A[6]), .A3(A[7]), .C(C));
endmodule

module Bit12_Register (
  input  [11:0] I,
  input  Load,
  input  INR,
  input  CLR,
  input  CP,
  input  Reset,
  output [11:0] A,
  output C
);

  wire bit4_register_1_c, bit4_register_2_c;

  Bit4_Register bit4_register_1 (
    .I0(I[0]), .I1(I[1]), .I2(I[2]), .I3(I[3]), .LD(Load), .CP(CP), .CLR(CLR), .INR(INR), .Reset(Reset),
    .A0(A[0]), .A1(A[1]), .A2(A[2]), .A3(A[3]), .C(bit4_register_1_c));
  Bit4_Register bit4_register_2 (
    .I0(I[4]), .I1(I[5]), .I2(I[6]), .I3(I[7]), .LD(Load), .CP(CP), .CLR(CLR), .INR(bit4_register_1_c),
    .Reset(Reset), .A0(A[4]), .A1(A[5]), .A2(A[6]), .A3(A[7]), .C(bit4_register_2_c));
  Bit4_Register bit4_register_3 (
    .I0(I[8]), .I1(I[9]), .I2(I[10]), .I3(I[11]), .LD(Load), .CP(CP), .CLR(CLR), .INR(bit4_register_2_c),
    .Reset(Reset), .A0(A[8]), .A1(A[9]), .A2(A[10]), .A3(A[11]), .C(C));
endmodule

module Bit16_Register (
  input  [15:0] I,
  input  Load,
  input  INR,
  input  CLR,
  input  CP,
  input  Reset,
  output [15:0] A,
  output C
);

  wire bit4_register_1_c, bit4_register_2_c, bit4_register_3_c;

  Bit4_Register bit4_register_1 (
    .I0(I[0]), .I1(I[1]), .I2(I[2]), .I3(I[3]), .LD(Load), .CP(CP), .CLR(CLR), .INR(INR), .Reset(Reset),
    .A0(A[0]), .A1(A[1]), .A2(A[2]), .A3(A[3]), .C(bit4_register_1_c));
  Bit4_Register bit4_register_2 (
    .I0(I[4]), .I1(I[5]), .I2(I[6]), .I3(I[7]), .LD(Load), .CP(CP), .CLR(CLR), .INR(bit4_register_1_c),
    .Reset(Reset), .A0(A[4]), .A1(A[5]), .A2(A[6]), .A3(A[7]), .C(bit4_register_2_c));
  Bit4_Register bit4_register_3 (
    .I0(I[8]), .I1(I[9]), .I2(I[10]), .I3(I[11]), .LD(Load), .CP(CP), .CLR(CLR), .INR(bit4_register_2_c),
    .Reset(Reset), .A0(A[8]), .A1(A[9]), .A2(A[10]), .A3(A[11]), .C(bit4_register_3_c));
  Bit4_Register bit4_register_4 (
    .I0(I[12]), .I1(I[13]), .I2(I[14]), .I3(I[15]), .LD(Load), .CP(CP), .CLR(CLR), .INR(bit4_register_3_c),
    .Reset(Reset), .A0(A[12]), .A1(A[13]), .A2(A[14]), .A3(A[15]), .C(C));
endmodule

module Bit4_Register (
  input  I0,
  input  I1,
  input  I2,
  input  I3,
  input  LD,
  input  CP,
  input  CLR,
  input  INR,
  input  Reset,
  output A0,
  output A1,
  output A2,
  output A3,
  output C
);

  wire and_1_out, and_2_out, and_3_out, and_4_out, and_5_out, and_6_out, and_7_out, and_8_out, and_9_out,
       and_10_out, and_11_out, and_12_out, and_13_out, and_15_out, and_16_out, and_17_out, and_18_out,
       not_1_out, not_2_out, not_3_out, not_4_out, not_5_out, not_6_out, not_7_out, or_1_out, or_2_out,
       or_3_out, or_4_out, or_5_out, or_6_out, or_7_out, or_8_out, or_9_out, or_10_out, or_11_out, or_12_out;

  not not_1 (not_1_out, I0);
  not not_2 (not_2_out, I1);
  not not_3 (not_3_out, I2);
  not not_4 (not_4_out, I3);
  not not_5 (not_5_out, CLR);
  not not_6 (not_6_out, LD);
  and and_1 (and_1_out, LD, not_5_out);
  and and_2 (and_2_out, and_1_out, I0);
  and and_3 (and_3_out, and_1_out, not_1_out);
  and and_4 (and_4_out, and_1_out, I1);
  and and_5 (and_5_out, and_1_out, not_2_out);
  and and_6 (and_6_out, and_1_out, I2);
  and and_7 (and_7_out, and_1_out, not_3_out);
  and and_8 (and_8_out, and_1_out, I3);
  and and_9 (and_9_out, and_1_out, not_4_out);
  and and_10 (and_10_out, not_6_out, INR, not_5_out);
  and and_11 (and_11_out, and_10_out, A0);
  and and_12 (and_12_out, and_11_out, A1);
  and and_13 (and_13_out, and_12_out, A2);
  and and_14 (C, and_13_out, A3);
  or or_1 (or_1_out, and_10_out, and_2_out);
  or or_2 (or_2_out, and_3_out, and_10_out);
  or or_3 (or_3_out, and_11_out, and_4_out);
  or or_4 (or_4_out, and_5_out, and_11_out);
  or or_5 (or_5_out, and_12_out, and_6_out);
  or or_6 (or_6_out, and_7_out, and_12_out);
  or or_7 (or_7_out, and_13_out, and_8_out);
  or or_8 (or_8_out, and_9_out, and_13_out);
  not not_7 (not_7_out, CLR);
  and and_15 (and_15_out, not_7_out, or_1_out);
  or or_9 (or_9_out, or_2_out, CLR);
  and and_16 (and_16_out, not_7_out, or_3_out);
  or or_10 (or_10_out, or_4_out, CLR);
  and and_17 (and_17_out, not_7_out, or_5_out);
  or or_11 (or_11_out, or_6_out, CLR);
  and and_18 (and_18_out, not_7_out, or_7_out);
  or or_12 (or_12_out, or_8_out, CLR);
  // Master_Slave_Flip_Flop master_slave_flip_flop_1: pin names not known; wires that end beside it: and_15_out, CP, or_9_out, Reset, A0
  // Master_Slave_Flip_Flop master_slave_flip_flop_2: pin names not known; wires that end beside it: and_16_out, CP, or_10_out, Reset, A1
  // Master_Slave_Flip_Flop master_slave_flip_flop_3: pin names not known; wires that end beside it: and_17_out, CP, or_11_out, Reset, A2
  // Master_Slave_Flip_Flop master_slave_flip_flop_4: pin names not known; wires that end beside it: and_18_out, CP, or_12_out, Reset, A3
endmodule
