// Logisim project JAndKFlipFlop.circ as structural Verilog: 1 circuit, main circuit main
module main (
  input  in_1,
  input  in_2,
  input  in_3,
  input  in_4,
  input  in_5,
  input  in_6,
  input  in_7,
  input  in_8,
  input  in_9,
  input  in_10,
  output out_11,
  output out_12,
  output out_13,
  output out_14,
  output out_15,
  output out_16,
  output out_17,
  output out_18
);

  wire clock_1_out, clock_2_out, clock_3_out, dipswitch_1_p1, dipswitch_1_p2, nand_1_out, nand_2_out,
       nand_3_out, nand_4_out, nand_5_out, nand_6_out, nand_7_out, nand_8_out, nand_9_out, nand_16_out,
       nand_17_out, nand_18_out, nand_19_out, nand_20_out, nand_21_out, nand_22_out, nand_23_out,
       nand_24_out, not_1_out, not_2_out;

  Clock clock_1 (.out(clock_1_out));
  // DipSwitch dipswitch_1: pin names not known; wires that end beside it: dipswitch_1_p1, dipswitch_1_p2
  Clock clock_2 (.out(clock_2_out));
  nand nand_1 (nand_1_out, nand_16_out, dipswitch_1_p1, clock_1_out);
  nand nand_2 (nand_2_out, clock_1_out, dipswitch_1_p2, nand_9_out);
  nand nand_3 (nand_3_out, in_2, clock_2_out);
  nand nand_4 (nand_4_out, clock_2_out, in_4);
  nand nand_5 (nand_5_out, in_5, in_6);
  nand nand_6 (nand_6_out, in_6, in_7);
  nand nand_7 (nand_7_out, in_8, in_9);
  nand nand_8 (nand_8_out, in_9, in_8);
  nand nand_9 (nand_9_out, nand_1_out, nand_16_out);
  nand nand_10 (out_12, nand_3_out, out_14);
  nand nand_11 (out_14, out_12, nand_4_out);
  nand nand_12 (in_7, nand_5_out, in_5);
  nand nand_13 (in_5, in_7, nand_6_out);
  nand nand_14 (in_8, nand_7_out, in_8);
  nand nand_15 (in_8, in_8, nand_8_out);
  nand nand_16 (nand_16_out, nand_9_out, nand_2_out);
  Clock clock_3 (.out(clock_3_out));
  LED led_1 (.in(nand_9_out));
  LED led_2 (.in(nand_16_out));
  nand nand_17 (nand_17_out, in_1, clock_3_out);
  nand nand_18 (nand_18_out, clock_3_out, in_1);
  nand nand_19 (nand_19_out, nand_17_out, nand_20_out);
  nand nand_20 (nand_20_out, nand_19_out, nand_18_out);
  not not_1 (not_1_out, in_9);
  not not_2 (not_2_out, clock_3_out);
  nand nand_21 (nand_21_out, in_8, not_1_out);
  nand nand_22 (nand_22_out, not_1_out, in_8);
  nand nand_23 (nand_23_out, nand_19_out, not_2_out);
  nand nand_24 (nand_24_out, not_2_out, nand_20_out);
  nand nand_25 (in_8, nand_21_out, in_8);
  nand nand_26 (in_8, in_8, nand_22_out);
  nand nand_27 (out_11, nand_23_out, in_1);
  nand nand_28 (in_1, out_11, nand_24_out);

  assign in_3 = in_1;
  assign in_10 = in_8;
  assign out_13 = in_1;
  assign out_15 = in_7;
  assign out_16 = in_5;
  assign out_17 = in_8;
  assign out_18 = in_8;
endmodule
