// Logisim project MasterSlaveJKFF.circ as structural Verilog: 3 circuits, main circuit main
module main (
  input  J,
  input  K,
  input  in_3,
  input  in_4,
  output Q,
  output QB,
  output out_7,
  output out_8
);

  wire clock_1_out, clock_2_out, nand_1_out, nand_2_out, nand_3_out, nand_4_out, nand_5_out, nand_6_out,
       nand_7_out, nand_8_out, nand_9_out, nand_10_out, nand_11_out, nand_12_out, nand_13_out, nand_14_out,
       undriven;

  Clock clock_1 (.out(clock_1_out));
  Clock clock_2 (.out(clock_2_out));
  nand nand_1 (nand_1_out, QB, J, clock_1_out);
  nand nand_2 (nand_2_out, clock_1_out, K, Q);
  nand nand_3 (nand_3_out, 1'b0, in_3, clock_2_out);
  nand nand_4 (nand_4_out, clock_2_out, in_4, undriven);
  nand nand_5 (nand_5_out, clock_2_out, clock_2_out);
  nand nand_6 (nand_6_out, clock_1_out, clock_1_out);
  nand nand_7 (nand_7_out, nand_3_out, nand_8_out);
  nand nand_8 (nand_8_out, nand_7_out, nand_4_out);
  nand nand_9 (nand_9_out, nand_1_out, nand_10_out);
  nand nand_10 (nand_10_out, nand_9_out, nand_2_out);
  nand nand_11 (nand_11_out, nand_5_out, nand_7_out);
  nand nand_12 (nand_12_out, nand_8_out, nand_5_out);
  nand nand_13 (nand_13_out, nand_6_out, nand_9_out);
  nand nand_14 (nand_14_out, nand_10_out, nand_6_out);
  nand nand_15 (Q, nand_13_out, QB);
  nand nand_16 (QB, Q, nand_14_out);
  nand nand_17 (out_7, nand_11_out, out_8);
  nand nand_18 (out_8, out_7, nand_12_out);
endmodule

module JK (
  input  J,
  input  K,
  input  CP,
  output Q,
  output QBar
);

  wire nand_1_out, nand_2_out;

  nand nand_1 (nand_1_out, J, CP);
  nand nand_2 (nand_2_out, CP, K);
  nand nand_3 (Q, nand_1_out, QBar);
  nand nand_4 (QBar, Q, nand_2_out);
endmodule

module MasterSlaveJK (
  input  J,
  input  K,
  output Q,
  output QBar
);

  wire clock_1_out, jk_1_q, jk_1_qbar, not_1_out;

  Clock clock_1 (.out(clock_1_out));
  not not_1 (not_1_out, clock_1_out);
  JK jk_1 (.J(J), .K(K), .CP(clock_1_out), .Q(jk_1_q), .QBar(jk_1_qbar));
  JK jk_2 (.J(jk_1_q), .K(jk_1_qbar), .CP(not_1_out), .Q(Q), .QBar(QBar));
endmodule
