// Logisim project TwoXoneMux.circ as structural Verilog: 1 circuit, main circuit twoXoneMultiplexer
module twoXoneMultiplexer (
  input  I0,
  input  I1,
  input  S0,
  output Y
);

  wire and_1_out, and_2_out, not_1_out;

  not not_1 (not_1_out, S0);
  and and_1 (and_1_out, not_1_out, I0);
  and and_2 (and_2_out, S0, I1);
  or or_1 (Y, and_1_out, and_2_out);
endmodule
