// Logisim project fourXoneFromTwoXoneMux.circ as structural Verilog: 1 circuit, main circuit main
module main (
  input  I0,
  input  I1,
  input  I2,
  input  I3,
  input  S1,
  input  S0,
  output Y
);

  wire twoxonemultiplexer_1_y, twoxonemultiplexer_2_y;

  twoXoneMultiplexer twoxonemultiplexer_1 (.I0(I0), .I1(I1), .S0(S0), .Y(twoxonemultiplexer_1_y));
  twoXoneMultiplexer twoxonemultiplexer_2 (.I0(I2), .I1(I3), .S0(S0), .Y(twoxonemultiplexer_2_y));
  twoXoneMultiplexer twoxonemultiplexer_3 (.I0(twoxonemultiplexer_1_y), .I1(twoxonemultiplexer_2_y), .S0(S1), .Y(Y));
endmodule
